// Logisim project Circuitos-M1.circ as structural Verilog: 22 circuits, main circuit Calculadora_Completa
module main (
  input  [15:0] in_1,
  input  [15:0] in_2
);

  wire and_1_out, and_2_out, and_3_out, and_4_out, button_2_out, button_3_out, button_4_out, button_out,
       display_7_segmentos_1_s0, display_7_segmentos_1_s1, display_7_segmentos_1_s2,
       display_7_segmentos_1_s3, display_7_segmentos_1_s4, display_7_segmentos_1_s5,
       display_7_segmentos_1_s6, display_7_segmentos_2_s0, display_7_segmentos_2_s1,
       display_7_segmentos_2_s2, display_7_segmentos_2_s3, display_7_segmentos_2_s4,
       display_7_segmentos_2_s5, display_7_segmentos_2_s6, display_7_segmentos_3_s0,
       display_7_segmentos_3_s1, display_7_segmentos_3_s2, display_7_segmentos_3_s3,
       display_7_segmentos_3_s4, display_7_segmentos_3_s5, display_7_segmentos_3_s6,
       display_7_segmentos_4_s0, display_7_segmentos_4_s1, display_7_segmentos_4_s2,
       display_7_segmentos_4_s3, display_7_segmentos_4_s4, display_7_segmentos_4_s5,
       display_7_segmentos_4_s6, not_1_out, not_2_out, not_3_out, not_4_out, or_1_out;
  wire [1:0] botao_1_out_5;
  wire [3:0] separador_binario_1_out_2, separador_binario_1_out_3, separador_binario_1_out_4,
       separador_binario_1_out_5;
  wire [15:0] controlled_buffer_1_out, controlled_buffer_2_out, controlled_buffer_3_out,
       controlled_buffer_4_out, controlled_buffer_5_out, controlled_buffer_6_out, controlled_buffer_7_out,
       controlled_buffer_8_out, controlled_buffer_9_out, diminuidor_16_bits_1_out_3, divider_1_out,
       multiplicador_completo_1_out_3, somador_de_16_bits_16_1_out_4;

  Button button (.out(button_out));
  Button button_2 (.out(button_2_out));
  Button button_3 (.out(button_3_out));
  Button button_4 (.out(button_4_out));
  or or_1 (or_1_out, button_4_out, button_3_out, button_2_out, button_out);
  Botao botao_1 (
    .out_5(botao_1_out_5), .in_1(button_4_out), .in_2(button_3_out), .in_3(button_2_out), .in_4(button_out));
  Display_7_segmentos display_7_segmentos_1 (
    .in_1(separador_binario_1_out_2), .S0(display_7_segmentos_1_s0), .S1(display_7_segmentos_1_s1),
    .S2(display_7_segmentos_1_s2), .S3(display_7_segmentos_1_s3), .S4(display_7_segmentos_1_s4),
    .S5(display_7_segmentos_1_s5), .S6(display_7_segmentos_1_s6));
  not not_1 (not_1_out, botao_1_out_5[0]);
  not not_2 (not_2_out, botao_1_out_5[1]);
  not not_3 (not_3_out, botao_1_out_5[1]);
  not not_4 (not_4_out, botao_1_out_5[0]);
  _7_Segment_Display u_7_segment_display_1 (
    .g(display_7_segmentos_1_s5), .f(display_7_segmentos_1_s6), .a(display_7_segmentos_1_s0),
    .b(display_7_segmentos_1_s1), .e(display_7_segmentos_1_s4), .d(display_7_segmentos_1_s3),
    .c(display_7_segmentos_1_s2));  // open: dp
  and and_1 (and_1_out, not_1_out, or_1_out, not_2_out);
  and and_2 (and_2_out, botao_1_out_5[0], or_1_out, not_3_out);
  and and_3 (and_3_out, not_4_out, or_1_out, botao_1_out_5[1]);
  and and_4 (and_4_out, botao_1_out_5[1], or_1_out, botao_1_out_5[0]);
  Display_7_segmentos display_7_segmentos_2 (
    .in_1(separador_binario_1_out_3), .S0(display_7_segmentos_2_s0), .S1(display_7_segmentos_2_s1),
    .S2(display_7_segmentos_2_s2), .S3(display_7_segmentos_2_s3), .S4(display_7_segmentos_2_s4),
    .S5(display_7_segmentos_2_s5), .S6(display_7_segmentos_2_s6));
  _7_Segment_Display u_7_segment_display_2 (
    .g(display_7_segmentos_2_s5), .f(display_7_segmentos_2_s6), .a(display_7_segmentos_2_s0),
    .b(display_7_segmentos_2_s1), .e(display_7_segmentos_2_s4), .d(display_7_segmentos_2_s3),
    .c(display_7_segmentos_2_s2));  // open: dp
  assign controlled_buffer_1_out = and_1_out ? in_1 : 16'bz;  // Controlled_Buffer controlled_buffer_1
  assign controlled_buffer_2_out = and_1_out ? in_2 : 16'bz;  // Controlled_Buffer controlled_buffer_2
  assign controlled_buffer_3_out = and_2_out ? in_1 : 16'bz;  // Controlled_Buffer controlled_buffer_3
  assign controlled_buffer_4_out = and_2_out ? in_2 : 16'bz;  // Controlled_Buffer controlled_buffer_4
  assign controlled_buffer_5_out = and_3_out ? in_1 : 16'bz;  // Controlled_Buffer controlled_buffer_5
  assign controlled_buffer_6_out = and_3_out ? in_2 : 16'bz;  // Controlled_Buffer controlled_buffer_6
  assign controlled_buffer_7_out = and_4_out ? in_1 : 16'bz;  // Controlled_Buffer controlled_buffer_7
  assign controlled_buffer_8_out = and_4_out ? in_2 : 16'bz;  // Controlled_Buffer controlled_buffer_8
  Somador_de_16_bits__16 somador_de_16_bits_16_1 (
    .in_1(controlled_buffer_1_out), .in_2(controlled_buffer_2_out), .out_4(somador_de_16_bits_16_1_out_4));  // open: out_3
  Diminuidor_16_bits diminuidor_16_bits_1 (
    .in_1(controlled_buffer_3_out), .in_2(controlled_buffer_4_out), .out_3(diminuidor_16_bits_1_out_3));
  Multiplicador_Completo multiplicador_completo_1 (
    .in_1(controlled_buffer_5_out), .in_2(controlled_buffer_6_out), .out_3(multiplicador_completo_1_out_3));
  Divider #(.width(16)) divider_1 (
    .a(controlled_buffer_7_out), .b(controlled_buffer_8_out), .out(divider_1_out));  // open: upper, rem
  Display_7_segmentos display_7_segmentos_3 (
    .in_1(separador_binario_1_out_4), .S0(display_7_segmentos_3_s0), .S1(display_7_segmentos_3_s1),
    .S2(display_7_segmentos_3_s2), .S3(display_7_segmentos_3_s3), .S4(display_7_segmentos_3_s4),
    .S5(display_7_segmentos_3_s5), .S6(display_7_segmentos_3_s6));
  _7_Segment_Display u_7_segment_display_3 (
    .g(display_7_segmentos_3_s5), .f(display_7_segmentos_3_s6), .a(display_7_segmentos_3_s0),
    .b(display_7_segmentos_3_s1), .e(display_7_segmentos_3_s4), .d(display_7_segmentos_3_s3),
    .c(display_7_segmentos_3_s2));  // open: dp
  assign controlled_buffer_9_out = and_1_out ? somador_de_16_bits_16_1_out_4 : 16'bz;  // Controlled_Buffer controlled_buffer_9
  assign controlled_buffer_9_out = and_2_out ? diminuidor_16_bits_1_out_3 : 16'bz;  // Controlled_Buffer controlled_buffer_10
  assign controlled_buffer_9_out = and_3_out ? multiplicador_completo_1_out_3 : 16'bz;  // Controlled_Buffer controlled_buffer_11
  assign controlled_buffer_9_out = and_4_out ? divider_1_out : 16'bz;  // Controlled_Buffer controlled_buffer_12
  Display_7_segmentos display_7_segmentos_4 (
    .in_1(separador_binario_1_out_5), .S0(display_7_segmentos_4_s0), .S1(display_7_segmentos_4_s1),
    .S2(display_7_segmentos_4_s2), .S3(display_7_segmentos_4_s3), .S4(display_7_segmentos_4_s4),
    .S5(display_7_segmentos_4_s5), .S6(display_7_segmentos_4_s6));
  Separador_Binario separador_binario_1 (
    .in_1(controlled_buffer_9_out), .out_2(separador_binario_1_out_2), .out_3(separador_binario_1_out_3),
    .out_4(separador_binario_1_out_4), .out_5(separador_binario_1_out_5));
  _7_Segment_Display u_7_segment_display_4 (
    .g(display_7_segmentos_4_s5), .f(display_7_segmentos_4_s6), .a(display_7_segmentos_4_s0),
    .b(display_7_segmentos_4_s1), .e(display_7_segmentos_4_s4), .d(display_7_segmentos_4_s3),
    .c(display_7_segmentos_4_s2));  // open: dp
endmodule

module Meio__Somador (
  input  A,
  input  B,
  output out_3,
  output out_4
);

  and and_1 (out_3, A, B);
  xor xor_1 (out_4, A, B);
endmodule

module Somador_Completo (
  input  A,
  input  B,
  input  C,
  output out_4,
  output out_5
);

  wire and_1_out, and_2_out, xor_1_out, xor_2_out;

  xor xor_1 (xor_1_out, A, B);
  xor xor_2 (xor_2_out, B, C);
  xor xor_3 (out_4, xor_1_out, C);
  and and_1 (and_1_out, C, B);
  and and_2 (and_2_out, A, xor_2_out);
  or or_1 (out_5, and_1_out, and_2_out);
endmodule

module Somador_8_bits (
  input  [7:0] in_1,
  input  [7:0] in_2,
  output [8:0] out_3
);

  wire meio_somador_1_out_3, somador_completo_2_out_5, somador_completo_3_out_5, somador_completo_4_out_5,
       somador_completo_5_out_5, somador_completo_6_out_5, somador_completo_7_out_5;

  Somador_Completo somador_completo_1 (
    .A(somador_completo_2_out_5), .B(in_1[7]), .C(in_2[7]), .out_4(out_3[7]), .out_5(out_3[8]));
  Somador_Completo somador_completo_2 (
    .A(somador_completo_3_out_5), .B(in_1[6]), .C(in_2[6]), .out_4(out_3[6]), .out_5(somador_completo_2_out_5));
  Somador_Completo somador_completo_3 (
    .A(somador_completo_4_out_5), .B(in_1[5]), .C(in_2[5]), .out_4(out_3[5]), .out_5(somador_completo_3_out_5));
  Somador_Completo somador_completo_4 (
    .A(somador_completo_5_out_5), .B(in_1[4]), .C(in_2[4]), .out_4(out_3[4]), .out_5(somador_completo_4_out_5));
  Somador_Completo somador_completo_5 (
    .A(somador_completo_7_out_5), .B(in_1[3]), .C(in_2[3]), .out_4(out_3[3]), .out_5(somador_completo_5_out_5));
  Somador_Completo somador_completo_6 (
    .A(meio_somador_1_out_3), .B(in_1[1]), .C(in_2[1]), .out_4(out_3[1]), .out_5(somador_completo_6_out_5));
  Somador_Completo somador_completo_7 (
    .A(somador_completo_6_out_5), .B(in_1[2]), .C(in_2[2]), .out_4(out_3[2]), .out_5(somador_completo_7_out_5));
  Meio__Somador meio_somador_1 (.A(in_1[0]), .B(in_2[0]), .out_3(meio_somador_1_out_3), .out_4(out_3[0]));
endmodule

module Somador_de_16_bits (
  input  [7:0] in_1,
  input  [7:0] in_2,
  input  [7:0] in_3,
  input  [7:0] in_4,
  output [9:0] out_5
);

  wire meio_somador_1_out_3, somador_completo_2_out_5, somador_completo_3_out_5, somador_completo_4_out_5,
       somador_completo_5_out_5, somador_completo_6_out_5, somador_completo_7_out_5, somador_completo_8_out_5;
  wire [8:0] somador_8_bits_1_out_3, somador_8_bits_2_out_3;

  Somador_8_bits somador_8_bits_1 (.in_1(in_1), .in_2(in_2), .out_3(somador_8_bits_1_out_3));
  Somador_8_bits somador_8_bits_2 (.in_1(in_3), .in_2(in_4), .out_3(somador_8_bits_2_out_3));
  Somador_Completo somador_completo_1 (
    .A(somador_completo_3_out_5), .B(somador_8_bits_1_out_3[8]), .C(somador_8_bits_2_out_3[8]),
    .out_4(out_5[8]), .out_5(out_5[9]));
  Somador_Completo somador_completo_2 (
    .A(somador_completo_5_out_5), .B(somador_8_bits_1_out_3[6]), .C(somador_8_bits_2_out_3[6]),
    .out_4(out_5[6]), .out_5(somador_completo_2_out_5));
  Somador_Completo somador_completo_3 (
    .A(somador_completo_2_out_5), .B(somador_8_bits_1_out_3[7]), .C(somador_8_bits_2_out_3[7]),
    .out_4(out_5[7]), .out_5(somador_completo_3_out_5));
  Somador_Completo somador_completo_4 (
    .A(somador_completo_6_out_5), .B(somador_8_bits_1_out_3[4]), .C(somador_8_bits_2_out_3[4]),
    .out_4(out_5[4]), .out_5(somador_completo_4_out_5));
  Somador_Completo somador_completo_5 (
    .A(somador_completo_4_out_5), .B(somador_8_bits_1_out_3[5]), .C(somador_8_bits_2_out_3[5]),
    .out_4(out_5[5]), .out_5(somador_completo_5_out_5));
  Somador_Completo somador_completo_6 (
    .A(somador_completo_8_out_5), .B(somador_8_bits_1_out_3[3]), .C(somador_8_bits_2_out_3[3]),
    .out_4(out_5[3]), .out_5(somador_completo_6_out_5));
  Somador_Completo somador_completo_7 (
    .A(meio_somador_1_out_3), .B(somador_8_bits_1_out_3[1]), .C(somador_8_bits_2_out_3[1]), .out_4(out_5[1]),
    .out_5(somador_completo_7_out_5));
  Somador_Completo somador_completo_8 (
    .A(somador_completo_7_out_5), .B(somador_8_bits_1_out_3[2]), .C(somador_8_bits_2_out_3[2]),
    .out_4(out_5[2]), .out_5(somador_completo_8_out_5));
  Meio__Somador meio_somador_1 (
    .A(somador_8_bits_1_out_3[0]), .B(somador_8_bits_2_out_3[0]), .out_3(meio_somador_1_out_3),
    .out_4(out_5[0]));
endmodule

module Somador_de_32_bits (
  input  [7:0] in_1,
  input  [7:0] in_2,
  input  [7:0] in_3,
  input  [7:0] in_4,
  input  [7:0] in_5,
  input  [7:0] in_6,
  input  [7:0] in_7,
  input  [7:0] in_8,
  output [10:0] out_9
);

  wire meio_somador_1_out_3, somador_completo_1_out_5, somador_completo_3_out_5, somador_completo_4_out_5,
       somador_completo_5_out_5, somador_completo_6_out_5, somador_completo_7_out_5,
       somador_completo_8_out_5, somador_completo_9_out_5;
  wire [9:0] somador_de_16_bits_1_out_5, somador_de_16_bits_2_out_5;

  Somador_de_16_bits somador_de_16_bits_1 (
    .in_1(in_1), .in_2(in_2), .in_3(in_3), .in_4(in_4), .out_5(somador_de_16_bits_1_out_5));
  Somador_de_16_bits somador_de_16_bits_2 (
    .in_1(in_5), .in_2(in_6), .in_3(in_7), .in_4(in_8), .out_5(somador_de_16_bits_2_out_5));
  Somador_Completo somador_completo_1 (
    .A(somador_completo_3_out_5), .B(somador_de_16_bits_1_out_5[8]), .C(somador_de_16_bits_2_out_5[8]),
    .out_4(out_9[8]), .out_5(somador_completo_1_out_5));
  Somador_Completo somador_completo_2 (
    .A(somador_completo_1_out_5), .B(somador_de_16_bits_1_out_5[9]), .C(somador_de_16_bits_2_out_5[9]),
    .out_4(out_9[9]), .out_5(out_9[10]));
  Somador_Completo somador_completo_3 (
    .A(somador_completo_4_out_5), .B(somador_de_16_bits_1_out_5[7]), .C(somador_de_16_bits_2_out_5[7]),
    .out_4(out_9[7]), .out_5(somador_completo_3_out_5));
  Somador_Completo somador_completo_4 (
    .A(somador_completo_5_out_5), .B(somador_de_16_bits_1_out_5[6]), .C(somador_de_16_bits_2_out_5[6]),
    .out_4(out_9[6]), .out_5(somador_completo_4_out_5));
  Somador_Completo somador_completo_5 (
    .A(somador_completo_7_out_5), .B(somador_de_16_bits_1_out_5[5]), .C(somador_de_16_bits_2_out_5[5]),
    .out_4(out_9[5]), .out_5(somador_completo_5_out_5));
  Somador_Completo somador_completo_6 (
    .A(somador_completo_8_out_5), .B(somador_de_16_bits_1_out_5[3]), .C(somador_de_16_bits_2_out_5[3]),
    .out_4(out_9[3]), .out_5(somador_completo_6_out_5));
  Somador_Completo somador_completo_7 (
    .A(somador_completo_6_out_5), .B(somador_de_16_bits_1_out_5[4]), .C(somador_de_16_bits_2_out_5[4]),
    .out_4(out_9[4]), .out_5(somador_completo_7_out_5));
  Somador_Completo somador_completo_8 (
    .A(somador_completo_9_out_5), .B(somador_de_16_bits_1_out_5[2]), .C(somador_de_16_bits_2_out_5[2]),
    .out_4(out_9[2]), .out_5(somador_completo_8_out_5));
  Somador_Completo somador_completo_9 (
    .A(meio_somador_1_out_3), .B(somador_de_16_bits_1_out_5[1]), .C(somador_de_16_bits_2_out_5[1]),
    .out_4(out_9[1]), .out_5(somador_completo_9_out_5));
  Meio__Somador meio_somador_1 (
    .A(somador_de_16_bits_1_out_5[0]), .B(somador_de_16_bits_2_out_5[0]), .out_3(meio_somador_1_out_3),
    .out_4(out_9[0]));
endmodule

module Somador_de_64_bits (
  input  [7:0] in_1,
  input  [7:0] in_2,
  input  [7:0] in_3,
  input  [7:0] in_4,
  input  [7:0] in_5,
  input  [7:0] in_6,
  input  [7:0] in_7,
  input  [7:0] in_8,
  input  [7:0] in_9,
  input  [7:0] in_10,
  input  [7:0] in_11,
  input  [7:0] in_12,
  input  [7:0] in_13,
  input  [7:0] in_14,
  input  [7:0] in_15,
  input  [7:0] in_16,
  output [11:0] out_17
);

  wire meio_somador_1_out_3, somador_completo_2_out_5, somador_completo_3_out_5, somador_completo_4_out_5,
       somador_completo_5_out_5, somador_completo_6_out_5, somador_completo_7_out_5,
       somador_completo_8_out_5, somador_completo_9_out_5, somador_completo_10_out_5;
  wire [10:0] somador_de_32_bits_1_out_9, somador_de_32_bits_2_out_9;

  Somador_de_32_bits somador_de_32_bits_1 (
    .in_1(in_1), .in_2(in_2), .in_3(in_3), .in_4(in_4), .in_5(in_5), .in_6(in_6), .in_7(in_7), .in_8(in_8),
    .out_9(somador_de_32_bits_1_out_9));
  Somador_de_32_bits somador_de_32_bits_2 (
    .in_1(in_9), .in_2(in_10), .in_3(in_11), .in_4(in_12), .in_5(in_13), .in_6(in_14), .in_7(in_15),
    .in_8(in_16), .out_9(somador_de_32_bits_2_out_9));
  Somador_Completo somador_completo_1 (
    .A(somador_completo_2_out_5), .B(somador_de_32_bits_1_out_9[10]), .C(somador_de_32_bits_2_out_9[10]),
    .out_4(out_17[10]), .out_5(out_17[11]));
  Somador_Completo somador_completo_2 (
    .A(somador_completo_3_out_5), .B(somador_de_32_bits_1_out_9[9]), .C(somador_de_32_bits_2_out_9[9]),
    .out_4(out_17[9]), .out_5(somador_completo_2_out_5));
  Somador_Completo somador_completo_3 (
    .A(somador_completo_4_out_5), .B(somador_de_32_bits_1_out_9[8]), .C(somador_de_32_bits_2_out_9[8]),
    .out_4(out_17[8]), .out_5(somador_completo_3_out_5));
  Somador_Completo somador_completo_4 (
    .A(somador_completo_6_out_5), .B(somador_de_32_bits_1_out_9[7]), .C(somador_de_32_bits_2_out_9[7]),
    .out_4(out_17[7]), .out_5(somador_completo_4_out_5));
  Somador_Completo somador_completo_5 (
    .A(somador_completo_7_out_5), .B(somador_de_32_bits_1_out_9[5]), .C(somador_de_32_bits_2_out_9[5]),
    .out_4(out_17[5]), .out_5(somador_completo_5_out_5));
  Somador_Completo somador_completo_6 (
    .A(somador_completo_5_out_5), .B(somador_de_32_bits_1_out_9[6]), .C(somador_de_32_bits_2_out_9[6]),
    .out_4(out_17[6]), .out_5(somador_completo_6_out_5));
  Somador_Completo somador_completo_7 (
    .A(somador_completo_8_out_5), .B(somador_de_32_bits_1_out_9[4]), .C(somador_de_32_bits_2_out_9[4]),
    .out_4(out_17[4]), .out_5(somador_completo_7_out_5));
  Somador_Completo somador_completo_8 (
    .A(somador_completo_9_out_5), .B(somador_de_32_bits_1_out_9[3]), .C(somador_de_32_bits_2_out_9[3]),
    .out_4(out_17[3]), .out_5(somador_completo_8_out_5));
  Somador_Completo somador_completo_9 (
    .A(somador_completo_10_out_5), .B(somador_de_32_bits_1_out_9[2]), .C(somador_de_32_bits_2_out_9[2]),
    .out_4(out_17[2]), .out_5(somador_completo_9_out_5));
  Meio__Somador meio_somador_1 (
    .A(somador_de_32_bits_1_out_9[0]), .B(somador_de_32_bits_2_out_9[0]), .out_3(meio_somador_1_out_3),
    .out_4(out_17[0]));
  Somador_Completo somador_completo_10 (
    .A(meio_somador_1_out_3), .B(somador_de_32_bits_1_out_9[1]), .C(somador_de_32_bits_2_out_9[1]),
    .out_4(out_17[1]), .out_5(somador_completo_10_out_5));
endmodule

module Somador_de_128_bits (
  input  [7:0] in_1,
  input  [7:0] in_2,
  input  [7:0] in_3,
  input  [7:0] in_4,
  input  [7:0] in_5,
  input  [7:0] in_6,
  input  [7:0] in_7,
  input  [7:0] in_8,
  input  [7:0] in_9,
  input  [7:0] in_10,
  input  [7:0] in_11,
  input  [7:0] in_12,
  input  [7:0] in_13,
  input  [7:0] in_14,
  input  [7:0] in_15,
  input  [7:0] in_16,
  input  [7:0] in_17,
  input  [7:0] in_18,
  input  [7:0] in_19,
  input  [7:0] in_20,
  input  [7:0] in_21,
  input  [7:0] in_22,
  input  [7:0] in_23,
  input  [7:0] in_24,
  input  [7:0] in_25,
  input  [7:0] in_26,
  input  [7:0] in_27,
  input  [7:0] in_28,
  input  [7:0] in_29,
  input  [7:0] in_30,
  input  [7:0] in_31,
  input  [7:0] in_32,
  output [12:0] out_33
);

  wire meio_somador_1_out_3, somador_completo_2_out_5, somador_completo_3_out_5, somador_completo_4_out_5,
       somador_completo_5_out_5, somador_completo_6_out_5, somador_completo_7_out_5,
       somador_completo_8_out_5, somador_completo_9_out_5, somador_completo_10_out_5,
       somador_completo_11_out_5;
  wire [11:0] somador_de_64_bits_1_out_17, somador_de_64_bits_2_out_17;

  Somador_de_64_bits somador_de_64_bits_1 (
    .in_1(in_1), .in_2(in_2), .in_3(in_3), .in_4(in_4), .in_5(in_5), .in_6(in_6), .in_7(in_7), .in_8(in_8),
    .in_9(in_9), .in_10(in_10), .in_11(in_11), .in_12(in_12), .in_13(in_13), .in_14(in_14), .in_15(in_15),
    .in_16(in_16), .out_17(somador_de_64_bits_1_out_17));
  Somador_de_64_bits somador_de_64_bits_2 (
    .in_1(in_17), .in_2(in_18), .in_3(in_19), .in_4(in_20), .in_5(in_21), .in_6(in_22), .in_7(in_23),
    .in_8(in_24), .in_9(in_25), .in_10(in_26), .in_11(in_27), .in_12(in_28), .in_13(in_29), .in_14(in_30),
    .in_15(in_31), .in_16(in_32), .out_17(somador_de_64_bits_2_out_17));
  Somador_Completo somador_completo_1 (
    .A(somador_completo_2_out_5), .B(somador_de_64_bits_1_out_17[11]), .C(somador_de_64_bits_2_out_17[11]),
    .out_4(out_33[11]), .out_5(out_33[12]));
  Somador_Completo somador_completo_2 (
    .A(somador_completo_3_out_5), .B(somador_de_64_bits_1_out_17[10]), .C(somador_de_64_bits_2_out_17[10]),
    .out_4(out_33[10]), .out_5(somador_completo_2_out_5));
  Somador_Completo somador_completo_3 (
    .A(somador_completo_5_out_5), .B(somador_de_64_bits_1_out_17[9]), .C(somador_de_64_bits_2_out_17[9]),
    .out_4(out_33[9]), .out_5(somador_completo_3_out_5));
  Somador_Completo somador_completo_4 (
    .A(somador_completo_6_out_5), .B(somador_de_64_bits_1_out_17[7]), .C(somador_de_64_bits_2_out_17[7]),
    .out_4(out_33[7]), .out_5(somador_completo_4_out_5));
  Somador_Completo somador_completo_5 (
    .A(somador_completo_4_out_5), .B(somador_de_64_bits_1_out_17[8]), .C(somador_de_64_bits_2_out_17[8]),
    .out_4(out_33[8]), .out_5(somador_completo_5_out_5));
  Somador_Completo somador_completo_6 (
    .A(somador_completo_8_out_5), .B(somador_de_64_bits_1_out_17[6]), .C(somador_de_64_bits_2_out_17[6]),
    .out_4(out_33[6]), .out_5(somador_completo_6_out_5));
  Somador_Completo somador_completo_7 (
    .A(somador_completo_9_out_5), .B(somador_de_64_bits_1_out_17[4]), .C(somador_de_64_bits_2_out_17[4]),
    .out_4(out_33[4]), .out_5(somador_completo_7_out_5));
  Somador_Completo somador_completo_8 (
    .A(somador_completo_7_out_5), .B(somador_de_64_bits_1_out_17[5]), .C(somador_de_64_bits_2_out_17[5]),
    .out_4(out_33[5]), .out_5(somador_completo_8_out_5));
  Somador_Completo somador_completo_9 (
    .A(somador_completo_10_out_5), .B(somador_de_64_bits_1_out_17[3]), .C(somador_de_64_bits_2_out_17[3]),
    .out_4(out_33[3]), .out_5(somador_completo_9_out_5));
  Somador_Completo somador_completo_10 (
    .A(somador_completo_11_out_5), .B(somador_de_64_bits_1_out_17[2]), .C(somador_de_64_bits_2_out_17[2]),
    .out_4(out_33[2]), .out_5(somador_completo_10_out_5));
  Somador_Completo somador_completo_11 (
    .A(meio_somador_1_out_3), .B(somador_de_64_bits_1_out_17[1]), .C(somador_de_64_bits_2_out_17[1]),
    .out_4(out_33[1]), .out_5(somador_completo_11_out_5));
  Meio__Somador meio_somador_1 (
    .A(somador_de_64_bits_1_out_17[0]), .B(somador_de_64_bits_2_out_17[0]), .out_3(meio_somador_1_out_3),
    .out_4(out_33[0]));
endmodule

module Inversor (
  input  [15:0] in_1,
  output [15:0] out_2
);

  not not_1 (out_2[0], in_1[0]);
  not not_2 (out_2[1], in_1[1]);
  not not_3 (out_2[2], in_1[2]);
  not not_4 (out_2[3], in_1[3]);
  not not_5 (out_2[4], in_1[4]);
  not not_6 (out_2[5], in_1[5]);
  not not_7 (out_2[6], in_1[6]);
  not not_8 (out_2[7], in_1[7]);
  not not_9 (out_2[8], in_1[8]);
  not not_10 (out_2[9], in_1[9]);
  not not_11 (out_2[10], in_1[10]);
  not not_12 (out_2[11], in_1[11]);
  not not_13 (out_2[12], in_1[12]);
  not not_14 (out_2[13], in_1[13]);
  not not_15 (out_2[14], in_1[14]);
  not not_16 (out_2[15], in_1[15]);
endmodule

module C2 (
  input  [15:0] in_1,
  input  [15:0] in_2,
  input  in_3,
  output out_4,
  output out_5,
  output out_6,
  output [15:0] out_7
);

  wire [15:0] inversor_1_out_2, somador_de_16_bits_16_1_out_4, somador_de_16_bits_16_2_out_4,
       somador_de_16_bits_16_3_out_4;

  Somador_de_16_bits__16 somador_de_16_bits_16_1 (
    .in_1(in_1), .in_2(in_2), .out_4(somador_de_16_bits_16_1_out_4), .out_3(out_4));
  Somador_de_16_bits__16 somador_de_16_bits_16_2 (
    .in_1(16'h1), .in_2(inversor_1_out_2), .out_4(somador_de_16_bits_16_2_out_4), .out_3(out_5));
  Inversor inversor_1 (.in_1(in_2), .out_2(inversor_1_out_2));
  Somador_de_16_bits__16 somador_de_16_bits_16_3 (
    .in_1(in_1), .in_2(somador_de_16_bits_16_2_out_4), .out_4(somador_de_16_bits_16_3_out_4), .out_3(out_6));
  BitSelector #(.width(32), .group(16)) bitselector_1 (
    .in({somador_de_16_bits_16_3_out_4, somador_de_16_bits_16_1_out_4}), .out(out_7), .sel(in_3));
endmodule

module Somador_de_16_bits__16 (
  input  [15:0] in_1,
  input  [15:0] in_2,
  output out_3,
  output [15:0] out_4
);

  wire meio_somador_1_out_3, somador_completo_2_out_5, somador_completo_3_out_5, somador_completo_4_out_5,
       somador_completo_5_out_5, somador_completo_6_out_5, somador_completo_7_out_5,
       somador_completo_8_out_5, somador_completo_9_out_5, somador_completo_10_out_5,
       somador_completo_11_out_5, somador_completo_12_out_5, somador_completo_13_out_5,
       somador_completo_14_out_5, somador_completo_15_out_5;

  Somador_Completo somador_completo_1 (
    .A(somador_completo_2_out_5), .B(in_1[15]), .C(in_2[15]), .out_4(out_4[15]), .out_5(out_3));
  Somador_Completo somador_completo_2 (
    .A(somador_completo_3_out_5), .B(in_1[14]), .C(in_2[14]), .out_4(out_4[14]),
    .out_5(somador_completo_2_out_5));
  Somador_Completo somador_completo_3 (
    .A(somador_completo_4_out_5), .B(in_1[13]), .C(in_2[13]), .out_4(out_4[13]),
    .out_5(somador_completo_3_out_5));
  Somador_Completo somador_completo_4 (
    .A(somador_completo_6_out_5), .B(in_1[12]), .C(in_2[12]), .out_4(out_4[12]),
    .out_5(somador_completo_4_out_5));
  Somador_Completo somador_completo_5 (
    .A(somador_completo_8_out_5), .B(in_1[10]), .C(in_2[10]), .out_4(out_4[10]),
    .out_5(somador_completo_5_out_5));
  Somador_Completo somador_completo_6 (
    .A(somador_completo_5_out_5), .B(in_1[11]), .C(in_2[11]), .out_4(out_4[11]),
    .out_5(somador_completo_6_out_5));
  Somador_Completo somador_completo_7 (
    .A(somador_completo_10_out_5), .B(in_1[8]), .C(in_2[8]), .out_4(out_4[8]),
    .out_5(somador_completo_7_out_5));
  Somador_Completo somador_completo_8 (
    .A(somador_completo_7_out_5), .B(in_1[9]), .C(in_2[9]), .out_4(out_4[9]), .out_5(somador_completo_8_out_5));
  Somador_Completo somador_completo_9 (
    .A(somador_completo_11_out_5), .B(in_1[6]), .C(in_2[6]), .out_4(out_4[6]),
    .out_5(somador_completo_9_out_5));
  Somador_Completo somador_completo_10 (
    .A(somador_completo_9_out_5), .B(in_1[7]), .C(in_2[7]), .out_4(out_4[7]),
    .out_5(somador_completo_10_out_5));
  Somador_Completo somador_completo_11 (
    .A(somador_completo_12_out_5), .B(in_1[5]), .C(in_2[5]), .out_4(out_4[5]),
    .out_5(somador_completo_11_out_5));
  Somador_Completo somador_completo_12 (
    .A(somador_completo_14_out_5), .B(in_1[4]), .C(in_2[4]), .out_4(out_4[4]),
    .out_5(somador_completo_12_out_5));
  Somador_Completo somador_completo_13 (
    .A(somador_completo_15_out_5), .B(in_1[2]), .C(in_2[2]), .out_4(out_4[2]),
    .out_5(somador_completo_13_out_5));
  Somador_Completo somador_completo_14 (
    .A(somador_completo_13_out_5), .B(in_1[3]), .C(in_2[3]), .out_4(out_4[3]),
    .out_5(somador_completo_14_out_5));
  Meio__Somador meio_somador_1 (.A(in_1[0]), .B(in_2[0]), .out_3(meio_somador_1_out_3), .out_4(out_4[0]));
  Somador_Completo somador_completo_15 (
    .A(meio_somador_1_out_3), .B(in_1[1]), .C(in_2[1]), .out_4(out_4[1]), .out_5(somador_completo_15_out_5));
endmodule

module Calculadora_Completa (
  input  [15:0] in_1,
  input  [15:0] in_2
);

  wire and_1_out, and_2_out, and_3_out, and_4_out, button_2_out, button_3_out, button_4_out, button_out,
       display_7_segmentos_1_s0, display_7_segmentos_1_s1, display_7_segmentos_1_s2,
       display_7_segmentos_1_s3, display_7_segmentos_1_s4, display_7_segmentos_1_s5,
       display_7_segmentos_1_s6, display_7_segmentos_2_s0, display_7_segmentos_2_s1,
       display_7_segmentos_2_s2, display_7_segmentos_2_s3, display_7_segmentos_2_s4,
       display_7_segmentos_2_s5, display_7_segmentos_2_s6, display_7_segmentos_3_s0,
       display_7_segmentos_3_s1, display_7_segmentos_3_s2, display_7_segmentos_3_s3,
       display_7_segmentos_3_s4, display_7_segmentos_3_s5, display_7_segmentos_3_s6,
       display_7_segmentos_4_s0, display_7_segmentos_4_s1, display_7_segmentos_4_s2,
       display_7_segmentos_4_s3, display_7_segmentos_4_s4, display_7_segmentos_4_s5,
       display_7_segmentos_4_s6, not_1_out, not_2_out, not_3_out, not_4_out, or_1_out;
  wire [1:0] botao_1_out_5;
  wire [3:0] separador_binario_1_out_2, separador_binario_1_out_3, separador_binario_1_out_4,
       separador_binario_1_out_5;
  wire [15:0] controlled_buffer_1_out, controlled_buffer_2_out, controlled_buffer_3_out,
       controlled_buffer_4_out, controlled_buffer_5_out, controlled_buffer_6_out, controlled_buffer_7_out,
       controlled_buffer_8_out, controlled_buffer_9_out, diminuidor_16_bits_1_out_3, divider_1_out,
       multiplicador_completo_1_out_3, somador_de_16_bits_16_1_out_4;

  Button button (.out(button_out));
  Button button_2 (.out(button_2_out));
  Button button_3 (.out(button_3_out));
  Button button_4 (.out(button_4_out));
  or or_1 (or_1_out, button_4_out, button_3_out, button_2_out, button_out);
  Botao botao_1 (
    .out_5(botao_1_out_5), .in_1(button_4_out), .in_2(button_3_out), .in_3(button_2_out), .in_4(button_out));
  Display_7_segmentos display_7_segmentos_1 (
    .in_1(separador_binario_1_out_2), .S0(display_7_segmentos_1_s0), .S1(display_7_segmentos_1_s1),
    .S2(display_7_segmentos_1_s2), .S3(display_7_segmentos_1_s3), .S4(display_7_segmentos_1_s4),
    .S5(display_7_segmentos_1_s5), .S6(display_7_segmentos_1_s6));
  not not_1 (not_1_out, botao_1_out_5[0]);
  not not_2 (not_2_out, botao_1_out_5[1]);
  not not_3 (not_3_out, botao_1_out_5[1]);
  not not_4 (not_4_out, botao_1_out_5[0]);
  _7_Segment_Display u_7_segment_display_1 (
    .g(display_7_segmentos_1_s5), .f(display_7_segmentos_1_s6), .a(display_7_segmentos_1_s0),
    .b(display_7_segmentos_1_s1), .e(display_7_segmentos_1_s4), .d(display_7_segmentos_1_s3),
    .c(display_7_segmentos_1_s2));  // open: dp
  and and_1 (and_1_out, not_1_out, or_1_out, not_2_out);
  and and_2 (and_2_out, botao_1_out_5[0], or_1_out, not_3_out);
  and and_3 (and_3_out, not_4_out, or_1_out, botao_1_out_5[1]);
  and and_4 (and_4_out, botao_1_out_5[1], or_1_out, botao_1_out_5[0]);
  Display_7_segmentos display_7_segmentos_2 (
    .in_1(separador_binario_1_out_3), .S0(display_7_segmentos_2_s0), .S1(display_7_segmentos_2_s1),
    .S2(display_7_segmentos_2_s2), .S3(display_7_segmentos_2_s3), .S4(display_7_segmentos_2_s4),
    .S5(display_7_segmentos_2_s5), .S6(display_7_segmentos_2_s6));
  _7_Segment_Display u_7_segment_display_2 (
    .g(display_7_segmentos_2_s5), .f(display_7_segmentos_2_s6), .a(display_7_segmentos_2_s0),
    .b(display_7_segmentos_2_s1), .e(display_7_segmentos_2_s4), .d(display_7_segmentos_2_s3),
    .c(display_7_segmentos_2_s2));  // open: dp
  assign controlled_buffer_1_out = and_1_out ? in_1 : 16'bz;  // Controlled_Buffer controlled_buffer_1
  assign controlled_buffer_2_out = and_1_out ? in_2 : 16'bz;  // Controlled_Buffer controlled_buffer_2
  assign controlled_buffer_3_out = and_2_out ? in_1 : 16'bz;  // Controlled_Buffer controlled_buffer_3
  assign controlled_buffer_4_out = and_2_out ? in_2 : 16'bz;  // Controlled_Buffer controlled_buffer_4
  assign controlled_buffer_5_out = and_3_out ? in_1 : 16'bz;  // Controlled_Buffer controlled_buffer_5
  assign controlled_buffer_6_out = and_3_out ? in_2 : 16'bz;  // Controlled_Buffer controlled_buffer_6
  assign controlled_buffer_7_out = and_4_out ? in_1 : 16'bz;  // Controlled_Buffer controlled_buffer_7
  assign controlled_buffer_8_out = and_4_out ? in_2 : 16'bz;  // Controlled_Buffer controlled_buffer_8
  Display_7_segmentos display_7_segmentos_3 (
    .in_1(separador_binario_1_out_4), .S0(display_7_segmentos_3_s0), .S1(display_7_segmentos_3_s1),
    .S2(display_7_segmentos_3_s2), .S3(display_7_segmentos_3_s3), .S4(display_7_segmentos_3_s4),
    .S5(display_7_segmentos_3_s5), .S6(display_7_segmentos_3_s6));
  Somador_de_16_bits__16 somador_de_16_bits_16_1 (
    .in_1(controlled_buffer_1_out), .in_2(controlled_buffer_2_out), .out_4(somador_de_16_bits_16_1_out_4));  // open: out_3
  Diminuidor_16_bits diminuidor_16_bits_1 (
    .in_1(controlled_buffer_3_out), .in_2(controlled_buffer_4_out), .out_3(diminuidor_16_bits_1_out_3));
  Multiplicador_Completo multiplicador_completo_1 (
    .in_1(controlled_buffer_5_out), .in_2(controlled_buffer_6_out), .out_3(multiplicador_completo_1_out_3));
  Divider #(.width(16)) divider_1 (
    .a(controlled_buffer_7_out), .b(controlled_buffer_8_out), .out(divider_1_out));  // open: upper, rem
  _7_Segment_Display u_7_segment_display_3 (
    .g(display_7_segmentos_3_s5), .f(display_7_segmentos_3_s6), .a(display_7_segmentos_3_s0),
    .b(display_7_segmentos_3_s1), .e(display_7_segmentos_3_s4), .d(display_7_segmentos_3_s3),
    .c(display_7_segmentos_3_s2));  // open: dp
  assign controlled_buffer_9_out = and_1_out ? somador_de_16_bits_16_1_out_4 : 16'bz;  // Controlled_Buffer controlled_buffer_9
  assign controlled_buffer_9_out = and_2_out ? diminuidor_16_bits_1_out_3 : 16'bz;  // Controlled_Buffer controlled_buffer_10
  assign controlled_buffer_9_out = and_3_out ? multiplicador_completo_1_out_3 : 16'bz;  // Controlled_Buffer controlled_buffer_11
  assign controlled_buffer_9_out = and_4_out ? divider_1_out : 16'bz;  // Controlled_Buffer controlled_buffer_12
  Display_7_segmentos display_7_segmentos_4 (
    .in_1(separador_binario_1_out_5), .S0(display_7_segmentos_4_s0), .S1(display_7_segmentos_4_s1),
    .S2(display_7_segmentos_4_s2), .S3(display_7_segmentos_4_s3), .S4(display_7_segmentos_4_s4),
    .S5(display_7_segmentos_4_s5), .S6(display_7_segmentos_4_s6));
  _7_Segment_Display u_7_segment_display_4 (
    .g(display_7_segmentos_4_s5), .f(display_7_segmentos_4_s6), .a(display_7_segmentos_4_s0),
    .b(display_7_segmentos_4_s1), .e(display_7_segmentos_4_s4), .d(display_7_segmentos_4_s3),
    .c(display_7_segmentos_4_s2));  // open: dp
  Separador_Binario separador_binario_1 (
    .in_1(controlled_buffer_9_out), .out_2(separador_binario_1_out_2), .out_3(separador_binario_1_out_3),
    .out_4(separador_binario_1_out_4), .out_5(separador_binario_1_out_5));

  // Notes on the sheet:
  //   INPUT DIVISOR
  //         INPUT MULTIPLICADOR
  //   INPUT SOMADOR
  //   INPUT 1
  //   INPUT 2
  //   BOTÃO
  //   INPUT SUBTRATOR
  //   SOMADOR
  //   DIVISOR
  //   SUBTRATOR
  //   MULTIPLICADOR
  //   SEPARADOR BINÁRIO
  //   OUTPUT'S
endmodule

module Botao (
  input  in_1,
  input  in_2,
  input  in_3,
  input  in_4,
  output [1:0] out_5
);

  wire and_1_out, and_2_out, not_1_out, not_2_out;

  not not_1 (not_1_out, in_1);
  not not_2 (not_2_out, in_4);
  and and_1 (and_1_out, not_1_out, in_2);
  and and_2 (and_2_out, in_3, not_2_out);
  or or_1 (out_5[0], and_1_out, in_4);
  or or_2 (out_5[1], and_2_out, in_4);
endmodule

module Diminuidor_16_bits (
  input  [15:0] in_1,
  input  [15:0] in_2,
  output [15:0] out_3
);

  wire [15:0] inversor_1_out_2, somador_de_16_bits_16_1_out_4;

  Inversor inversor_1 (.in_1(in_2), .out_2(inversor_1_out_2));
  Somador_de_16_bits__16 somador_de_16_bits_16_1 (
    .in_1(16'h1), .in_2(inversor_1_out_2), .out_4(somador_de_16_bits_16_1_out_4));  // open: out_3
  Somador_de_16_bits__16 somador_de_16_bits_16_2 (
    .in_1(in_1), .in_2(somador_de_16_bits_16_1_out_4), .out_4(out_3));  // open: out_3
endmodule

module Meio_Multiplicador (
  input  [15:0] in_1,
  input  [15:0] in_2,
  output [15:0] out_3,
  output [15:0] out_4,
  output [15:0] out_5,
  output [15:0] out_6,
  output [15:0] out_7,
  output [15:0] out_8,
  output [15:0] out_9,
  output [15:0] out_10,
  output [15:0] out_11,
  output [15:0] out_12,
  output [15:0] out_13,
  output [15:0] out_14,
  output [15:0] out_15,
  output [15:0] out_16,
  output [15:0] out_17,
  output [15:0] out_18
);

  wire [15:0] and_2_out_3, and_3_out_3, and_4_out_3, and_5_out_3, and_6_out_3, and_7_out_3, and_8_out_3,
       and_9_out_3, and_10_out_3, and_11_out_3, and_12_out_3, and_13_out_3, and_14_out_3, and_15_out_3,
       and_16_out_3, shifter_10_out, shifter_11_out, shifter_12_out, shifter_13_out, shifter_14_out,
       shifter_15_out;

  AND and_1 (.in_1(in_1), .in_2(in_2[0]), .out_3(out_3));
  AND and_2 (.in_1(in_1), .in_2(in_2[1]), .out_3(and_2_out_3));
  AND and_3 (.in_1(in_1), .in_2(in_2[2]), .out_3(and_3_out_3));
  AND and_4 (.in_1(in_1), .in_2(in_2[3]), .out_3(and_4_out_3));
  AND and_5 (.in_1(in_1), .in_2(in_2[4]), .out_3(and_5_out_3));
  AND and_6 (.in_1(in_1), .in_2(in_2[5]), .out_3(and_6_out_3));
  AND and_7 (.in_1(in_1), .in_2(in_2[6]), .out_3(and_7_out_3));
  AND and_8 (.in_1(in_1), .in_2(in_2[7]), .out_3(and_8_out_3));
  AND and_9 (.in_1(in_1), .in_2(in_2[8]), .out_3(and_9_out_3));
  AND and_10 (.in_1(in_1), .in_2(in_2[9]), .out_3(and_10_out_3));
  AND and_11 (.in_1(in_1), .in_2(in_2[10]), .out_3(and_11_out_3));
  AND and_12 (.in_1(in_1), .in_2(in_2[11]), .out_3(and_12_out_3));
  AND and_13 (.in_1(in_1), .in_2(in_2[12]), .out_3(and_13_out_3));
  AND and_14 (.in_1(in_1), .in_2(in_2[13]), .out_3(and_14_out_3));
  AND and_15 (.in_1(in_1), .in_2(in_2[14]), .out_3(and_15_out_3));
  AND and_16 (.in_1(in_1), .in_2(in_2[15]), .out_3(and_16_out_3));
  Shifter #(.width(16)) shifter_1 (.in(and_2_out_3), .\dist (4'b0001), .out(out_4));
  Shifter #(.width(16)) shifter_2 (.in(and_3_out_3), .\dist (4'b0010), .out(out_5));
  Shifter #(.width(16)) shifter_3 (.in(and_4_out_3), .\dist (4'b0011), .out(out_6));
  Shifter #(.width(16)) shifter_4 (.in(and_5_out_3), .\dist (4'b0100), .out(out_7));
  Shifter #(.width(16)) shifter_5 (.in(and_6_out_3), .\dist (4'b0101), .out(out_8));
  Shifter #(.width(16)) shifter_6 (.in(and_7_out_3), .\dist (4'b0110), .out(out_9));
  Shifter #(.width(16)) shifter_7 (.in(and_8_out_3), .\dist (4'b0111), .out(out_10));
  Shifter #(.width(16)) shifter_8 (.in(and_9_out_3), .\dist (4'b1000), .out(out_11));
  Shifter #(.width(16)) shifter_9 (.in(and_10_out_3), .\dist (4'b1001), .out(out_12));
  Shifter #(.width(16)) shifter_10 (.in(and_11_out_3), .\dist (4'b1001), .out(shifter_10_out));
  Shifter #(.width(16)) shifter_11 (.in(and_12_out_3), .\dist (4'b1001), .out(shifter_11_out));
  Shifter #(.width(16)) shifter_12 (.in(and_13_out_3), .\dist (4'b1001), .out(shifter_12_out));
  Shifter #(.width(16)) shifter_13 (.in(and_14_out_3), .\dist (4'b1001), .out(shifter_13_out));
  Shifter #(.width(16)) shifter_14 (.in(and_15_out_3), .\dist (4'b1001), .out(shifter_14_out));
  Shifter #(.width(16)) shifter_15 (.in(and_16_out_3), .\dist (4'b1001), .out(shifter_15_out));
  Shifter #(.width(16)) shifter_16 (.in(shifter_10_out), .\dist (4'b0001), .out(out_13));
  Shifter #(.width(16)) shifter_17 (.in(shifter_11_out), .\dist (4'b0010), .out(out_14));
  Shifter #(.width(16)) shifter_18 (.in(shifter_12_out), .\dist (4'b0011), .out(out_15));
  Shifter #(.width(16)) shifter_19 (.in(shifter_13_out), .\dist (4'b0100), .out(out_16));
  Shifter #(.width(16)) shifter_20 (.in(shifter_14_out), .\dist (4'b0101), .out(out_17));
  Shifter #(.width(16)) shifter_21 (.in(shifter_15_out), .\dist (4'b0110), .out(out_18));
endmodule

module AND (
  input  [15:0] in_1,
  input  in_2,
  output [15:0] out_3
);

  assign out_3 = in_1 & {16{in_2}};  // AND_Gate and_1, 16 bits wide
endmodule

module Somador_de_16_bits_completo_16 (
  input  in_1,
  input  [15:0] in_2,
  input  [15:0] in_3,
  output out_4,
  output [15:0] out_5
);

  wire somador_completo_2_out_5, somador_completo_3_out_5, somador_completo_4_out_5,
       somador_completo_5_out_5, somador_completo_6_out_5, somador_completo_7_out_5,
       somador_completo_8_out_5, somador_completo_9_out_5, somador_completo_10_out_5,
       somador_completo_11_out_5, somador_completo_12_out_5, somador_completo_13_out_5,
       somador_completo_14_out_5, somador_completo_15_out_5, somador_completo_16_out_5;

  Somador_Completo somador_completo_1 (
    .A(somador_completo_2_out_5), .B(in_2[15]), .C(in_3[15]), .out_4(out_5[15]), .out_5(out_4));
  Somador_Completo somador_completo_2 (
    .A(somador_completo_4_out_5), .B(in_2[14]), .C(in_3[14]), .out_4(out_5[14]),
    .out_5(somador_completo_2_out_5));
  Somador_Completo somador_completo_3 (
    .A(somador_completo_6_out_5), .B(in_2[12]), .C(in_3[12]), .out_4(out_5[12]),
    .out_5(somador_completo_3_out_5));
  Somador_Completo somador_completo_4 (
    .A(somador_completo_3_out_5), .B(in_2[13]), .C(in_3[13]), .out_4(out_5[13]),
    .out_5(somador_completo_4_out_5));
  Somador_Completo somador_completo_5 (
    .A(somador_completo_8_out_5), .B(in_2[10]), .C(in_3[10]), .out_4(out_5[10]),
    .out_5(somador_completo_5_out_5));
  Somador_Completo somador_completo_6 (
    .A(somador_completo_5_out_5), .B(in_2[11]), .C(in_3[11]), .out_4(out_5[11]),
    .out_5(somador_completo_6_out_5));
  Somador_Completo somador_completo_7 (
    .A(somador_completo_10_out_5), .B(in_2[8]), .C(in_3[8]), .out_4(out_5[8]),
    .out_5(somador_completo_7_out_5));
  Somador_Completo somador_completo_8 (
    .A(somador_completo_7_out_5), .B(in_2[9]), .C(in_3[9]), .out_4(out_5[9]), .out_5(somador_completo_8_out_5));
  Somador_Completo somador_completo_9 (
    .A(somador_completo_12_out_5), .B(in_2[6]), .C(in_3[6]), .out_4(out_5[6]),
    .out_5(somador_completo_9_out_5));
  Somador_Completo somador_completo_10 (
    .A(somador_completo_9_out_5), .B(in_2[7]), .C(in_3[7]), .out_4(out_5[7]),
    .out_5(somador_completo_10_out_5));
  Somador_Completo somador_completo_11 (
    .A(somador_completo_14_out_5), .B(in_2[4]), .C(in_3[4]), .out_4(out_5[4]),
    .out_5(somador_completo_11_out_5));
  Somador_Completo somador_completo_12 (
    .A(somador_completo_11_out_5), .B(in_2[5]), .C(in_3[5]), .out_4(out_5[5]),
    .out_5(somador_completo_12_out_5));
  Somador_Completo somador_completo_13 (
    .A(somador_completo_15_out_5), .B(in_2[2]), .C(in_3[2]), .out_4(out_5[2]),
    .out_5(somador_completo_13_out_5));
  Somador_Completo somador_completo_14 (
    .A(somador_completo_13_out_5), .B(in_2[3]), .C(in_3[3]), .out_4(out_5[3]),
    .out_5(somador_completo_14_out_5));
  Somador_Completo somador_completo_15 (
    .A(somador_completo_16_out_5), .B(in_2[1]), .C(in_3[1]), .out_4(out_5[1]),
    .out_5(somador_completo_15_out_5));
  Somador_Completo somador_completo_16 (
    .A(in_1), .B(in_2[0]), .C(in_3[0]), .out_4(out_5[0]), .out_5(somador_completo_16_out_5));
endmodule

module Multiplicador_Completo (
  input  [15:0] in_1,
  input  [15:0] in_2,
  output [15:0] out_3
);

  wire somador_de_16_bits_16_1_out_3, somador_de_16_bits_completo_16_1_out_4,
       somador_de_16_bits_completo_16_2_out_4, somador_de_16_bits_completo_16_3_out_4,
       somador_de_16_bits_completo_16_4_out_4, somador_de_16_bits_completo_16_5_out_4,
       somador_de_16_bits_completo_16_6_out_4, somador_de_16_bits_completo_16_7_out_4,
       somador_de_16_bits_completo_16_8_out_4, somador_de_16_bits_completo_16_9_out_4,
       somador_de_16_bits_completo_16_10_out_4, somador_de_16_bits_completo_16_11_out_4,
       somador_de_16_bits_completo_16_12_out_4, somador_de_16_bits_completo_16_13_out_4,
       somador_de_16_bits_completo_16_14_out_4;
  wire [15:0] meio_multiplicador_1_out_3, meio_multiplicador_1_out_4, meio_multiplicador_1_out_5,
       meio_multiplicador_1_out_6, meio_multiplicador_1_out_7, meio_multiplicador_1_out_8,
       meio_multiplicador_1_out_9, meio_multiplicador_1_out_10, meio_multiplicador_1_out_11,
       meio_multiplicador_1_out_12, meio_multiplicador_1_out_13, meio_multiplicador_1_out_14,
       meio_multiplicador_1_out_15, meio_multiplicador_1_out_16, meio_multiplicador_1_out_17,
       meio_multiplicador_1_out_18, somador_de_16_bits_16_1_out_4, somador_de_16_bits_completo_16_1_out_5,
       somador_de_16_bits_completo_16_3_out_5, somador_de_16_bits_completo_16_4_out_5,
       somador_de_16_bits_completo_16_5_out_5, somador_de_16_bits_completo_16_6_out_5,
       somador_de_16_bits_completo_16_7_out_5, somador_de_16_bits_completo_16_8_out_5,
       somador_de_16_bits_completo_16_9_out_5, somador_de_16_bits_completo_16_10_out_5,
       somador_de_16_bits_completo_16_11_out_5, somador_de_16_bits_completo_16_12_out_5,
       somador_de_16_bits_completo_16_13_out_5, somador_de_16_bits_completo_16_14_out_5;

  Somador_de_16_bits_completo_16 somador_de_16_bits_completo_16_1 (
    .in_1(somador_de_16_bits_completo_16_3_out_4), .in_2(somador_de_16_bits_completo_16_3_out_5),
    .in_3(meio_multiplicador_1_out_15), .out_5(somador_de_16_bits_completo_16_1_out_5),
    .out_4(somador_de_16_bits_completo_16_1_out_4));
  Somador_de_16_bits_completo_16 somador_de_16_bits_completo_16_2 (
    .in_1(somador_de_16_bits_completo_16_6_out_4), .in_2(somador_de_16_bits_completo_16_6_out_5),
    .in_3(meio_multiplicador_1_out_18), .out_5(out_3), .out_4(somador_de_16_bits_completo_16_2_out_4));
  Somador_de_16_bits_completo_16 somador_de_16_bits_completo_16_3 (
    .in_1(somador_de_16_bits_completo_16_4_out_4), .in_2(somador_de_16_bits_completo_16_4_out_5),
    .in_3(meio_multiplicador_1_out_14), .out_5(somador_de_16_bits_completo_16_3_out_5),
    .out_4(somador_de_16_bits_completo_16_3_out_4));
  Somador_de_16_bits_completo_16 somador_de_16_bits_completo_16_4 (
    .in_1(somador_de_16_bits_completo_16_7_out_4), .in_2(somador_de_16_bits_completo_16_7_out_5),
    .in_3(meio_multiplicador_1_out_13), .out_5(somador_de_16_bits_completo_16_4_out_5),
    .out_4(somador_de_16_bits_completo_16_4_out_4));
  Somador_de_16_bits_completo_16 somador_de_16_bits_completo_16_5 (
    .in_1(somador_de_16_bits_completo_16_1_out_4), .in_2(somador_de_16_bits_completo_16_1_out_5),
    .in_3(meio_multiplicador_1_out_16), .out_5(somador_de_16_bits_completo_16_5_out_5),
    .out_4(somador_de_16_bits_completo_16_5_out_4));
  Somador_de_16_bits_completo_16 somador_de_16_bits_completo_16_6 (
    .in_1(somador_de_16_bits_completo_16_5_out_4), .in_2(somador_de_16_bits_completo_16_5_out_5),
    .in_3(meio_multiplicador_1_out_17), .out_5(somador_de_16_bits_completo_16_6_out_5),
    .out_4(somador_de_16_bits_completo_16_6_out_4));
  Meio_Multiplicador meio_multiplicador_1 (
    .in_1(in_1), .in_2(in_2), .out_3(meio_multiplicador_1_out_3), .out_4(meio_multiplicador_1_out_4),
    .out_5(meio_multiplicador_1_out_5), .out_6(meio_multiplicador_1_out_6),
    .out_7(meio_multiplicador_1_out_7), .out_8(meio_multiplicador_1_out_8),
    .out_9(meio_multiplicador_1_out_9), .out_10(meio_multiplicador_1_out_10),
    .out_11(meio_multiplicador_1_out_11), .out_12(meio_multiplicador_1_out_12),
    .out_13(meio_multiplicador_1_out_13), .out_14(meio_multiplicador_1_out_14),
    .out_15(meio_multiplicador_1_out_15), .out_16(meio_multiplicador_1_out_16),
    .out_17(meio_multiplicador_1_out_17), .out_18(meio_multiplicador_1_out_18));
  Somador_de_16_bits_completo_16 somador_de_16_bits_completo_16_7 (
    .in_1(somador_de_16_bits_completo_16_8_out_4), .in_2(somador_de_16_bits_completo_16_8_out_5),
    .in_3(meio_multiplicador_1_out_12), .out_5(somador_de_16_bits_completo_16_7_out_5),
    .out_4(somador_de_16_bits_completo_16_7_out_4));
  Somador_de_16_bits_completo_16 somador_de_16_bits_completo_16_8 (
    .in_1(somador_de_16_bits_completo_16_9_out_4), .in_2(somador_de_16_bits_completo_16_9_out_5),
    .in_3(meio_multiplicador_1_out_11), .out_5(somador_de_16_bits_completo_16_8_out_5),
    .out_4(somador_de_16_bits_completo_16_8_out_4));
  Somador_de_16_bits_completo_16 somador_de_16_bits_completo_16_9 (
    .in_1(somador_de_16_bits_completo_16_10_out_4), .in_2(somador_de_16_bits_completo_16_10_out_5),
    .in_3(meio_multiplicador_1_out_10), .out_5(somador_de_16_bits_completo_16_9_out_5),
    .out_4(somador_de_16_bits_completo_16_9_out_4));
  Somador_de_16_bits_completo_16 somador_de_16_bits_completo_16_10 (
    .in_1(somador_de_16_bits_completo_16_11_out_4), .in_2(somador_de_16_bits_completo_16_11_out_5),
    .in_3(meio_multiplicador_1_out_9), .out_5(somador_de_16_bits_completo_16_10_out_5),
    .out_4(somador_de_16_bits_completo_16_10_out_4));
  Somador_de_16_bits_completo_16 somador_de_16_bits_completo_16_11 (
    .in_1(somador_de_16_bits_completo_16_12_out_4), .in_2(somador_de_16_bits_completo_16_12_out_5),
    .in_3(meio_multiplicador_1_out_8), .out_5(somador_de_16_bits_completo_16_11_out_5),
    .out_4(somador_de_16_bits_completo_16_11_out_4));
  Somador_de_16_bits_completo_16 somador_de_16_bits_completo_16_12 (
    .in_1(somador_de_16_bits_completo_16_14_out_4), .in_2(somador_de_16_bits_completo_16_14_out_5),
    .in_3(meio_multiplicador_1_out_7), .out_5(somador_de_16_bits_completo_16_12_out_5),
    .out_4(somador_de_16_bits_completo_16_12_out_4));
  Somador_de_16_bits_completo_16 somador_de_16_bits_completo_16_13 (
    .in_1(somador_de_16_bits_16_1_out_3), .in_2(somador_de_16_bits_16_1_out_4),
    .in_3(meio_multiplicador_1_out_5), .out_5(somador_de_16_bits_completo_16_13_out_5),
    .out_4(somador_de_16_bits_completo_16_13_out_4));
  Somador_de_16_bits_completo_16 somador_de_16_bits_completo_16_14 (
    .in_1(somador_de_16_bits_completo_16_13_out_4), .in_2(somador_de_16_bits_completo_16_13_out_5),
    .in_3(meio_multiplicador_1_out_6), .out_5(somador_de_16_bits_completo_16_14_out_5),
    .out_4(somador_de_16_bits_completo_16_14_out_4));
  Somador_de_16_bits__16 somador_de_16_bits_16_1 (
    .in_1(meio_multiplicador_1_out_3), .in_2(meio_multiplicador_1_out_4),
    .out_4(somador_de_16_bits_16_1_out_4), .out_3(somador_de_16_bits_16_1_out_3));
endmodule

module \Seletores_Operação  (
  output out_1,
  output out_2,
  output out_3,
  output out_4
);

  wire button_2_out, button_3_out, button_4_out, button_out, not_1_out, not_2_out, not_3_out, not_4_out,
       or_1_out;
  wire [1:0] botao_1_out_5;

  Button button (.out(button_out));
  Button button_2 (.out(button_2_out));
  Button button_3 (.out(button_3_out));
  Button button_4 (.out(button_4_out));
  Botao botao_1 (
    .out_5(botao_1_out_5), .in_1(button_out), .in_2(button_2_out), .in_3(button_3_out), .in_4(button_4_out));
  and and_1 (out_1, not_1_out, or_1_out, not_2_out);
  not not_1 (not_1_out, botao_1_out_5[0]);
  not not_2 (not_2_out, botao_1_out_5[1]);
  or or_1 (or_1_out, button_4_out, button_3_out, button_2_out, button_out);
  and and_2 (out_2, botao_1_out_5[0], or_1_out, not_3_out);
  not not_3 (not_3_out, botao_1_out_5[1]);
  and and_3 (out_3, not_4_out, or_1_out, botao_1_out_5[1]);
  not not_4 (not_4_out, botao_1_out_5[0]);
  and and_4 (out_4, botao_1_out_5[0], or_1_out, botao_1_out_5[1]);
endmodule

module Controlador_display (
  input  [3:0] in_1
);

  wire display_7_segmentos_1_p1, display_7_segmentos_1_p2, display_7_segmentos_1_p3,
       display_7_segmentos_1_p4, display_7_segmentos_1_p5, display_7_segmentos_1_p6, undriven;

  // Display_7_segmentos display_7_segmentos_1: pin names not known; wires that end beside it: display_7_segmentos_1_p1, display_7_segmentos_1_p2, display_7_segmentos_1_p3, display_7_segmentos_1_p4, display_7_segmentos_1_p5, display_7_segmentos_1_p6, display_7_segmentos_1_p6, display_7_segmentos_1_p6, display_7_segmentos_1_p6, display_7_segmentos_1_p6, display_7_segmentos_1_p6, display_7_segmentos_1_p6
  _7_Segment_Display u_7_segment_display_1 (
    .g(display_7_segmentos_1_p5), .f(undriven), .a(display_7_segmentos_1_p1), .b(display_7_segmentos_1_p2),
    .e(display_7_segmentos_1_p4), .d(display_7_segmentos_1_p3), .c(display_7_segmentos_1_p6));  // open: dp
  LED led_1 (.in(undriven));
  LED led_2 (.in(undriven));
  LED led_3 (.in(undriven));
  LED led_4 (.in(display_7_segmentos_1_p4));
  LED led_5 (.in(display_7_segmentos_1_p4));
  LED led_6 (.in(display_7_segmentos_1_p4));
  LED led_7 (.in(display_7_segmentos_1_p1));
  LED led_8 (.in(display_7_segmentos_1_p1));
  LED led_9 (.in(display_7_segmentos_1_p1));
  LED led_10 (.in(display_7_segmentos_1_p5));
  LED led_11 (.in(display_7_segmentos_1_p5));
  LED led_12 (.in(display_7_segmentos_1_p5));
  LED led_13 (.in(display_7_segmentos_1_p3));
  LED led_14 (.in(display_7_segmentos_1_p3));
  LED led_15 (.in(display_7_segmentos_1_p3));
  LED led_16 (.in(display_7_segmentos_1_p2));
  LED led_17 (.in(display_7_segmentos_1_p2));
  LED led_18 (.in(display_7_segmentos_1_p2));
  LED led_19 (.in(display_7_segmentos_1_p6));
  LED led_20 (.in(display_7_segmentos_1_p6));
  LED led_21 (.in(display_7_segmentos_1_p6));
endmodule

module Display_7_segmentos (
  input  [3:0] in_1,
  output S0,
  output S1,
  output S2,
  output S3,
  output S4,
  output S5,
  output S6
);

  wire and_1_out, and_2_out, and_3_out, and_4_out, and_5_out, and_6_out, and_7_out, and_8_out, and_9_out,
       and_10_out, not_1_out, not_2_out, not_3_out, not_4_out, not_5_out, not_6_out, not_7_out, not_8_out;

  not not_1 (not_1_out, in_1[2]);
  and and_1 (and_1_out, not_1_out, not_2_out);
  or or_1 (S0, in_1[3], in_1[1], and_1_out, and_2_out);
  not not_2 (not_2_out, in_1[0]);
  and and_2 (and_2_out, in_1[2], in_1[0]);
  or or_2 (S1, not_5_out, and_3_out, and_4_out);
  not not_3 (not_3_out, in_1[1]);
  not not_4 (not_4_out, in_1[0]);
  not not_5 (not_5_out, in_1[2]);
  and and_3 (and_3_out, not_3_out, not_4_out);
  not not_6 (not_6_out, in_1[1]);
  and and_4 (and_4_out, in_1[1], in_1[0]);
  and and_5 (and_5_out, in_1[1], not_7_out);
  or or_3 (S2, not_6_out, in_1[2], in_1[0]);
  or or_4 (S3, and_5_out, and_6_out, and_7_out, and_8_out, in_1[3]);
  not not_7 (not_7_out, in_1[0]);
  not not_8 (not_8_out, in_1[2]);
  and and_6 (and_6_out, not_8_out, not_7_out);
  or or_5 (S4, and_5_out, and_6_out);
  and and_7 (and_7_out, not_8_out, in_1[1]);
  or or_6 (S5, and_7_out, in_1[3], and_9_out, and_10_out);
  and and_8 (and_8_out, not_8_out, in_1[0], in_1[2]);
  or or_7 (S6, and_3_out, and_9_out, and_10_out, in_1[2]);
  and and_9 (and_9_out, in_1[2], not_3_out);
  and and_10 (and_10_out, not_7_out, in_1[2]);
endmodule

module Separador_Binario (
  input  [15:0] in_1,
  output [3:0] out_2,
  output [3:0] out_3,
  output [3:0] out_4,
  output [3:0] out_5
);

  wire [15:0] diminuidor_16_bits_1_out_3, diminuidor_16_bits_2_out_3, multiplicador_completo_1_out_3,
       multiplicador_completo_2_out_3, multiplicador_completo_3_out_3;
  wire [15:4] diminuidor_16_bits_3_out_3, divider_1_out, divider_2_out, divider_3_out;

  Divider #(.width(16)) divider_1 (.a(in_1), .b(16'h3e8), .out({divider_1_out, out_2}));  // open: upper, rem
  Multiplicador_Completo multiplicador_completo_1 (
    .in_1({divider_1_out, out_2}), .in_2(16'h3e8), .out_3(multiplicador_completo_1_out_3));
  Diminuidor_16_bits diminuidor_16_bits_1 (
    .in_1(in_1), .in_2(multiplicador_completo_1_out_3), .out_3(diminuidor_16_bits_1_out_3));
  Divider #(.width(16)) divider_2 (
    .a(diminuidor_16_bits_1_out_3), .b(16'h64), .out({divider_2_out, out_3}));  // open: upper, rem
  Multiplicador_Completo multiplicador_completo_2 (
    .in_1({divider_2_out, out_3}), .in_2(16'h64), .out_3(multiplicador_completo_2_out_3));
  Diminuidor_16_bits diminuidor_16_bits_2 (
    .in_1(diminuidor_16_bits_1_out_3), .in_2(multiplicador_completo_2_out_3),
    .out_3(diminuidor_16_bits_2_out_3));
  Multiplicador_Completo multiplicador_completo_3 (
    .in_1({divider_3_out, out_4}), .in_2(16'ha), .out_3(multiplicador_completo_3_out_3));
  Diminuidor_16_bits diminuidor_16_bits_3 (
    .in_1(diminuidor_16_bits_2_out_3), .in_2(multiplicador_completo_3_out_3),
    .out_3({diminuidor_16_bits_3_out_3, out_5}));
  Divider #(.width(16)) divider_3 (
    .a(diminuidor_16_bits_2_out_3), .b(16'ha), .out({divider_3_out, out_4}));  // open: upper, rem
endmodule
