// Logisim project Circuitos-M2.circ as structural Verilog: 10 circuits, main circuit main
module main (
  output [1:0] out_1,
  output [1:0] out_2
);

  wire and_1_out, and_2_out, and_3_out, and_4_out, button_1_out, clock_1_out, clock_2_out,
       comparador_1_out_66, controlled_buffer_1_out, controlled_buffer_2_out, controlled_buffer_3_out,
       controlled_buffer_4_out, not_1_out, not_2_out, or_1_out, or_2_out;
  wire [3:0] counter_1_q, counter_2_q, random_1_out, random_2_out;
  wire [15:0] comparador_1_out_34, comparador_1_out_35, comparador_1_out_36, comparador_1_out_37,
       comparador_1_out_38, comparador_1_out_39, comparador_1_out_40, comparador_1_out_41,
       comparador_1_out_42, comparador_1_out_43, comparador_1_out_44, comparador_1_out_45,
       comparador_1_out_46, comparador_1_out_47, comparador_1_out_48, comparador_1_out_49,
       comparador_1_out_50, comparador_1_out_51, comparador_1_out_52, comparador_1_out_53,
       comparador_1_out_54, comparador_1_out_55, comparador_1_out_56, comparador_1_out_57,
       comparador_1_out_58, comparador_1_out_59, comparador_1_out_60, comparador_1_out_61,
       comparador_1_out_62, comparador_1_out_63, comparador_1_out_64, comparador_1_out_65, decoder_1_out0,
       decoder_2_out0, demultiplexer_1_out0, demultiplexer_1_out1, demultiplexer_1_out2,
       demultiplexer_1_out3, demultiplexer_1_out4, demultiplexer_1_out5, demultiplexer_1_out6,
       demultiplexer_1_out7, demultiplexer_1_out8, demultiplexer_1_out9, demultiplexer_1_out10,
       demultiplexer_1_out11, demultiplexer_1_out12, demultiplexer_1_out13, demultiplexer_1_out14,
       demultiplexer_1_out15, demultiplexer_2_out0, demultiplexer_2_out1, demultiplexer_2_out2,
       demultiplexer_2_out3, demultiplexer_2_out4, demultiplexer_2_out5, demultiplexer_2_out6,
       demultiplexer_2_out7, demultiplexer_2_out8, demultiplexer_2_out9, demultiplexer_2_out10,
       demultiplexer_2_out11, demultiplexer_2_out12, demultiplexer_2_out13, demultiplexer_2_out14,
       demultiplexer_2_out15, somador_1_out_33, somador_1_out_34, somador_1_out_35, somador_1_out_36,
       somador_1_out_37, somador_1_out_38, somador_1_out_39, somador_1_out_40, somador_1_out_41,
       somador_1_out_42, somador_1_out_43, somador_1_out_44, somador_1_out_45, somador_1_out_46,
       somador_1_out_47, somador_1_out_48;

  Joystick_part #(.bits(2)) joystick_1 (.x(out_1), .y(out_2));
  Button button_1 (.out(button_1_out));
  not not_1 (not_1_out, out_1[1]);
  not not_2 (not_2_out, out_2[1]);
  Clock clock_1 (.out(clock_1_out));
  and and_1 (and_1_out, out_1[0], out_1[1]);
  and and_2 (and_2_out, out_1[0], not_1_out);
  Clock clock_2 (.out(clock_2_out));
  and and_3 (and_3_out, out_2[0], out_2[1]);
  and and_4 (and_4_out, out_2[0], not_2_out);
  assign controlled_buffer_1_out = and_1_out ? clock_1_out : 1'bz;  // Controlled_Buffer controlled_buffer_1
  assign controlled_buffer_2_out = or_1_out ? clock_1_out : 1'bz;  // Controlled_Buffer controlled_buffer_2
  or or_1 (or_1_out, and_1_out, and_2_out);
  assign controlled_buffer_3_out = and_4_out ? clock_2_out : 1'bz;  // Controlled_Buffer controlled_buffer_3
  assign controlled_buffer_4_out = or_2_out ? clock_2_out : 1'bz;  // Controlled_Buffer controlled_buffer_4
  or or_2 (or_2_out, and_3_out, and_4_out);
  Counter #(.width(4), .max('hf)) counter_1 (
    .load(controlled_buffer_1_out), .D(counter_1_q), .count(controlled_buffer_2_out), .Q(counter_1_q),
    .clk(controlled_buffer_2_out), .clr(button_1_out));  // open: carry
  Counter #(.width(4), .max('hf)) counter_2 (
    .load(controlled_buffer_3_out), .D(counter_2_q), .count(controlled_buffer_4_out), .Q(counter_2_q),
    .clk(controlled_buffer_4_out), .clr(button_1_out));  // open: carry
  Random #(.width(4)) random_1 (.clk(comparador_1_out_66), .out(random_1_out));  // open: next, clr
  Random #(.width(4)) random_2 (.clk(comparador_1_out_66), .out(random_2_out));  // open: next, clr
  Decoder #(.select(4)) decoder_1 (
    .out0(decoder_1_out0[0]), .out1(decoder_1_out0[1]), .out2(decoder_1_out0[2]), .out3(decoder_1_out0[3]),
    .out4(decoder_1_out0[4]), .out5(decoder_1_out0[5]), .out6(decoder_1_out0[6]), .out7(decoder_1_out0[7]),
    .out8(decoder_1_out0[8]), .out9(decoder_1_out0[9]), .out10(decoder_1_out0[10]),
    .out11(decoder_1_out0[11]), .out12(decoder_1_out0[12]), .out13(decoder_1_out0[13]),
    .out14(decoder_1_out0[14]), .out15(decoder_1_out0[15]), .sel(counter_1_q));  // open: en
  Decoder #(.select(4)) decoder_2 (
    .out0(decoder_2_out0[0]), .out1(decoder_2_out0[1]), .out2(decoder_2_out0[2]), .out3(decoder_2_out0[3]),
    .out4(decoder_2_out0[4]), .out5(decoder_2_out0[5]), .out6(decoder_2_out0[6]), .out7(decoder_2_out0[7]),
    .out8(decoder_2_out0[8]), .out9(decoder_2_out0[9]), .out10(decoder_2_out0[10]),
    .out11(decoder_2_out0[11]), .out12(decoder_2_out0[12]), .out13(decoder_2_out0[13]),
    .out14(decoder_2_out0[14]), .out15(decoder_2_out0[15]), .sel(random_1_out));  // open: en
  Demultiplexer #(.select(4), .width(16)) demultiplexer_1 (
    .out0(demultiplexer_1_out0), .out1(demultiplexer_1_out1), .out2(demultiplexer_1_out2),
    .out3(demultiplexer_1_out3), .out4(demultiplexer_1_out4), .out5(demultiplexer_1_out5),
    .out6(demultiplexer_1_out6), .out7(demultiplexer_1_out7), .out8(demultiplexer_1_out8),
    .out9(demultiplexer_1_out9), .out10(demultiplexer_1_out10), .out11(demultiplexer_1_out11),
    .out12(demultiplexer_1_out12), .out13(demultiplexer_1_out13), .out14(demultiplexer_1_out14),
    .out15(demultiplexer_1_out15), .in(decoder_1_out0), .sel(counter_2_q));  // open: en
  Demultiplexer #(.select(4), .width(16)) demultiplexer_2 (
    .out0(demultiplexer_2_out0), .out1(demultiplexer_2_out1), .out2(demultiplexer_2_out2),
    .out3(demultiplexer_2_out3), .out4(demultiplexer_2_out4), .out5(demultiplexer_2_out5),
    .out6(demultiplexer_2_out6), .out7(demultiplexer_2_out7), .out8(demultiplexer_2_out8),
    .out9(demultiplexer_2_out9), .out10(demultiplexer_2_out10), .out11(demultiplexer_2_out11),
    .out12(demultiplexer_2_out12), .out13(demultiplexer_2_out13), .out14(demultiplexer_2_out14),
    .out15(demultiplexer_2_out15), .in(decoder_2_out0), .sel(random_2_out));  // open: en
  Comparador comparador_1 (
    .in_1(demultiplexer_1_out0), .in_2(demultiplexer_2_out0), .in_3(demultiplexer_1_out1),
    .in_4(demultiplexer_2_out1), .in_5(demultiplexer_1_out2), .in_6(demultiplexer_2_out2),
    .in_7(demultiplexer_1_out3), .in_8(demultiplexer_2_out3), .in_9(demultiplexer_1_out4),
    .in_10(demultiplexer_2_out4), .in_11(demultiplexer_1_out5), .in_12(demultiplexer_2_out5),
    .in_13(demultiplexer_1_out6), .in_14(demultiplexer_2_out6), .in_15(demultiplexer_1_out7),
    .in_16(demultiplexer_2_out7), .in_17(demultiplexer_1_out8), .in_18(demultiplexer_2_out8),
    .in_19(demultiplexer_1_out9), .in_20(demultiplexer_2_out9), .in_21(demultiplexer_1_out10),
    .in_22(demultiplexer_2_out10), .in_23(demultiplexer_1_out11), .in_24(demultiplexer_2_out11),
    .in_25(demultiplexer_1_out12), .in_26(demultiplexer_2_out12), .in_27(demultiplexer_1_out13),
    .in_28(demultiplexer_2_out13), .in_29(demultiplexer_1_out14), .in_30(demultiplexer_2_out14),
    .in_31(demultiplexer_1_out15), .in_32(demultiplexer_2_out15), .out_34(comparador_1_out_34),
    .out_35(comparador_1_out_35), .out_36(comparador_1_out_36), .out_37(comparador_1_out_37),
    .out_38(comparador_1_out_38), .out_39(comparador_1_out_39), .out_40(comparador_1_out_40),
    .out_41(comparador_1_out_41), .out_42(comparador_1_out_42), .out_43(comparador_1_out_43),
    .out_44(comparador_1_out_44), .out_45(comparador_1_out_45), .out_46(comparador_1_out_46),
    .out_47(comparador_1_out_47), .out_48(comparador_1_out_48), .out_49(comparador_1_out_49),
    .out_50(comparador_1_out_50), .out_51(comparador_1_out_51), .out_52(comparador_1_out_52),
    .out_53(comparador_1_out_53), .out_54(comparador_1_out_54), .out_55(comparador_1_out_55),
    .out_56(comparador_1_out_56), .out_57(comparador_1_out_57), .out_58(comparador_1_out_58),
    .out_59(comparador_1_out_59), .out_60(comparador_1_out_60), .out_61(comparador_1_out_61),
    .out_62(comparador_1_out_62), .out_63(comparador_1_out_63), .out_64(comparador_1_out_64),
    .out_65(comparador_1_out_65), .in_33(counter_2_q), .out_66(comparador_1_out_66));
  Somador somador_1 (
    .in_1(comparador_1_out_34), .in_2(comparador_1_out_35), .in_3(comparador_1_out_36),
    .in_4(comparador_1_out_37), .in_5(comparador_1_out_38), .in_6(comparador_1_out_39),
    .in_7(comparador_1_out_40), .in_8(comparador_1_out_41), .in_9(comparador_1_out_42),
    .in_10(comparador_1_out_43), .in_11(comparador_1_out_44), .in_12(comparador_1_out_45),
    .in_13(comparador_1_out_46), .in_14(comparador_1_out_47), .in_15(comparador_1_out_48),
    .in_16(comparador_1_out_49), .in_17(comparador_1_out_50), .in_18(comparador_1_out_51),
    .in_19(comparador_1_out_52), .in_20(comparador_1_out_53), .in_21(comparador_1_out_54),
    .in_22(comparador_1_out_55), .in_23(comparador_1_out_56), .in_24(comparador_1_out_57),
    .in_25(comparador_1_out_58), .in_26(comparador_1_out_59), .in_27(comparador_1_out_60),
    .in_28(comparador_1_out_61), .in_29(comparador_1_out_62), .in_30(comparador_1_out_63),
    .in_31(comparador_1_out_64), .in_32(comparador_1_out_65), .out_33(somador_1_out_33),
    .out_34(somador_1_out_34), .out_35(somador_1_out_35), .out_36(somador_1_out_36),
    .out_37(somador_1_out_37), .out_38(somador_1_out_38), .out_39(somador_1_out_39),
    .out_40(somador_1_out_40), .out_41(somador_1_out_41), .out_42(somador_1_out_42),
    .out_43(somador_1_out_43), .out_44(somador_1_out_44), .out_45(somador_1_out_45),
    .out_46(somador_1_out_46), .out_47(somador_1_out_47), .out_48(somador_1_out_48));
  DotMatrix #(.inputtype("row"), .matrixcols(16), .matrixrows(16)) dotmatrix_1 (
    .row0(somador_1_out_33), .row1(somador_1_out_34), .row2(somador_1_out_35), .row3(somador_1_out_36),
    .row4(somador_1_out_37), .row5(somador_1_out_38), .row6(somador_1_out_39), .row7(somador_1_out_40),
    .row8(somador_1_out_41), .row9(somador_1_out_42), .row10(somador_1_out_43), .row11(somador_1_out_44),
    .row12(somador_1_out_45), .row13(somador_1_out_46), .row14(somador_1_out_47), .row15(somador_1_out_48));
endmodule

module Encoder_8_bits (
  output out_1,
  output out_2,
  output out_3,
  output out_4
);

  wire L_out, N_out, Ne_out, No_out, O_out, S_out, Se_out, So_out;

  Button No (.out(No_out));
  Button O (.out(O_out));
  Button So (.out(So_out));
  Button N (.out(N_out));
  Button Ne (.out(Ne_out));
  Button L (.out(L_out));
  Button Se (.out(Se_out));
  Button S (.out(S_out));
  or or_1 (out_2, No_out, O_out, So_out, S_out);
  or or_2 (out_3, No_out, O_out, Se_out, L_out);
  ExactlyOne xor_1 (
    .out(out_1), .in0(N_out), .in1(Ne_out), .in2(L_out), .in3(Se_out), .in4(S_out), .in5(So_out),
    .in6(O_out), .in7(No_out));
  or or_3 (out_4, No_out, So_out, Se_out, Ne_out);
endmodule

module Multiplexer (
  input  [15:0] in_1,
  input  [15:0] in_2,
  input  [15:0] in_3,
  input  [15:0] in_4,
  input  [15:0] in_5,
  input  [15:0] in_6,
  input  [15:0] in_7,
  input  [15:0] in_8,
  input  [2:0] in_9,
  output [18:0] out_10
);

  wire and_1_out, and_2_out, and_3_out, and_4_out, and_5_out, and_6_out, and_7_out, and_8_out, not_1_out,
       not_2_out, not_3_out, not_4_out, not_5_out, not_6_out, not_7_out, not_8_out, not_9_out, not_10_out,
       not_11_out, not_12_out;

  not not_1 (not_1_out, in_9[2]);
  assign out_10[15:0] = and_1_out ? in_1 : 16'bz;  // Controlled_Buffer controlled_buffer_1
  assign out_10[15:0] = and_2_out ? in_2 : 16'bz;  // Controlled_Buffer controlled_buffer_2
  and and_1 (and_1_out, not_1_out, not_3_out, not_5_out);
  and and_2 (and_2_out, not_6_out, not_2_out, in_9[0]);
  not not_2 (not_2_out, in_9[1]);
  not not_3 (not_3_out, in_9[1]);
  not not_4 (not_4_out, in_9[2]);
  not not_5 (not_5_out, in_9[0]);
  not not_6 (not_6_out, in_9[2]);
  assign out_10[15:0] = and_4_out ? in_3 : 16'bz;  // Controlled_Buffer controlled_buffer_3
  assign out_10[15:0] = and_3_out ? in_4 : 16'bz;  // Controlled_Buffer controlled_buffer_4
  and and_3 (and_3_out, not_7_out, in_9[1], in_9[0]);
  and and_4 (and_4_out, not_4_out, in_9[1], not_8_out);
  not not_7 (not_7_out, in_9[2]);
  not not_8 (not_8_out, in_9[0]);
  assign out_10[15:0] = and_6_out ? in_5 : 16'bz;  // Controlled_Buffer controlled_buffer_5
  assign out_10[15:0] = and_5_out ? in_6 : 16'bz;  // Controlled_Buffer controlled_buffer_6
  and and_5 (and_5_out, in_9[2], not_9_out, in_9[0]);
  and and_6 (and_6_out, in_9[2], not_11_out, not_10_out);
  not not_9 (not_9_out, in_9[1]);
  not not_10 (not_10_out, in_9[0]);
  not not_11 (not_11_out, in_9[1]);
  assign out_10[15:0] = and_8_out ? in_7 : 16'bz;  // Controlled_Buffer controlled_buffer_7
  assign out_10[15:0] = and_7_out ? in_8 : 16'bz;  // Controlled_Buffer controlled_buffer_8
  and and_7 (and_7_out, in_9[2], in_9[1], in_9[0]);
  and and_8 (and_8_out, in_9[2], in_9[1], not_12_out);
  not not_12 (not_12_out, in_9[0]);

  assign out_10[18:16] = in_9;
endmodule

module Demux (
  input  [18:0] in_1,
  output [15:0] out_2,
  output [15:0] out_3,
  output [15:0] out_4,
  output [15:0] out_5,
  output [15:0] out_6,
  output [15:0] out_7,
  output [15:0] out_8,
  output [15:0] out_9
);

  wire and_1_out, and_2_out, and_3_out, and_4_out, and_5_out, and_6_out, and_7_out, and_8_out, not_1_out,
       not_2_out, not_3_out, not_4_out, not_5_out, not_6_out, not_7_out, not_8_out, not_9_out, not_10_out,
       not_11_out, not_12_out;

  assign out_2 = and_1_out ? in_1[15:0] : 16'bz;  // Controlled_Buffer controlled_buffer_1
  assign out_3 = and_2_out ? in_1[15:0] : 16'bz;  // Controlled_Buffer controlled_buffer_2
  and and_1 (and_1_out, not_1_out, not_3_out, not_2_out);
  and and_2 (and_2_out, not_4_out, not_5_out, in_1[16]);
  not not_1 (not_1_out, in_1[18]);
  not not_2 (not_2_out, in_1[16]);
  not not_3 (not_3_out, in_1[17]);
  not not_4 (not_4_out, in_1[18]);
  not not_5 (not_5_out, in_1[17]);
  assign out_4 = and_4_out ? in_1[15:0] : 16'bz;  // Controlled_Buffer controlled_buffer_3
  assign out_5 = and_3_out ? in_1[15:0] : 16'bz;  // Controlled_Buffer controlled_buffer_4
  and and_3 (and_3_out, not_8_out, in_1[17], in_1[16]);
  and and_4 (and_4_out, not_6_out, in_1[17], not_7_out);
  not not_6 (not_6_out, in_1[18]);
  not not_7 (not_7_out, in_1[16]);
  not not_8 (not_8_out, in_1[18]);
  assign out_6 = and_6_out ? in_1[15:0] : 16'bz;  // Controlled_Buffer controlled_buffer_5
  assign out_7 = and_5_out ? in_1[15:0] : 16'bz;  // Controlled_Buffer controlled_buffer_6
  and and_5 (and_5_out, in_1[18], not_9_out, in_1[16]);
  and and_6 (and_6_out, in_1[18], not_10_out, not_11_out);
  not not_9 (not_9_out, in_1[17]);
  not not_10 (not_10_out, in_1[17]);
  not not_11 (not_11_out, in_1[16]);
  assign out_8 = and_8_out ? in_1[15:0] : 16'bz;  // Controlled_Buffer controlled_buffer_7
  assign out_9 = and_7_out ? in_1[15:0] : 16'bz;  // Controlled_Buffer controlled_buffer_8
  and and_7 (and_7_out, in_1[18], in_1[17], in_1[16]);
  and and_8 (and_8_out, in_1[18], in_1[17], not_12_out);
  not not_12 (not_12_out, in_1[16]);
endmodule

module multiplexer_do_logsim (
  input  [7:0] in_1,
  input  [7:0] in_2,
  input  [7:0] in_3,
  input  [7:0] in_4,
  input  [7:0] in_5,
  input  [7:0] in_6,
  input  [7:0] in_7,
  input  [7:0] in_8,
  input  \Subtração ,
  input  Habilitado,
  input  [2:0] in_11,
  input  in_12,
  output [7:0] out_13,
  output [7:0] out_14,
  output [7:0] out_15,
  output [7:0] out_16,
  output [7:0] out_17,
  output [7:0] out_18,
  output [7:0] out_19,
  output [7:0] out_20
);

  wire button_1_out, clock_1_out, clock_2_out, comparator_1_eq, comparator_1_gt, comparator_1_lt,
       counter_1_carry, demultiplexer_2_out0, demultiplexer_2_out1, demultiplexer_2_out2,
       demultiplexer_2_out3, demultiplexer_2_out4, demultiplexer_2_out5, demultiplexer_2_out6,
       demultiplexer_2_out7, or_1_out;
  wire [2:0] counter_1_q, counter_2_q;
  wire [7:0] demultiplexer_1_out0, demultiplexer_1_out1, demultiplexer_1_out2, demultiplexer_1_out3,
       demultiplexer_1_out4, demultiplexer_1_out5, demultiplexer_1_out6, demultiplexer_1_out7,
       multiplexer_1_out;

  Clock clock_1 (.out(clock_1_out));
  Multiplexer_part #(.select(3), .width(8)) multiplexer_1 (
    .in0(in_1), .in1(in_2), .in2(in_3), .in3(in_4), .in4(in_5), .in5(in_6), .in6(in_7), .in7(in_8),
    .out(multiplexer_1_out), .sel(counter_1_q));  // open: en
  Counter #(.width(3), .max('h7)) counter_1 (
    .load(\Subtração ), .count(Habilitado), .Q(counter_1_q), .carry(counter_1_carry), .clk(clock_1_out),
    .clr(or_1_out));  // open: D
  or or_1 (or_1_out, button_1_out, comparator_1_eq);
  Button button_1 (.out(button_1_out));
  Counter #(.width(3), .max('h7)) counter_2 (
    .Q(counter_2_q), .clk(counter_1_carry), .clr(button_1_out));  // open: load, D, count, carry
  Demultiplexer #(.select(3), .width(8)) demultiplexer_1 (
    .out0(demultiplexer_1_out0), .out1(demultiplexer_1_out1), .out2(demultiplexer_1_out2),
    .out3(demultiplexer_1_out3), .out4(demultiplexer_1_out4), .out5(demultiplexer_1_out5),
    .out6(demultiplexer_1_out6), .out7(demultiplexer_1_out7), .in(multiplexer_1_out), .sel(counter_1_q));  // open: en
  Comparator #(.width(3), .mode("unsigned")) comparator_1 (
    .a(counter_2_q), .b(in_11), .gt(comparator_1_gt), .eq(comparator_1_eq), .lt(comparator_1_lt));
  Demultiplexer #(.select(3)) demultiplexer_2 (
    .out0(demultiplexer_2_out0), .out1(demultiplexer_2_out1), .out2(demultiplexer_2_out2),
    .out3(demultiplexer_2_out3), .out4(demultiplexer_2_out4), .out5(demultiplexer_2_out5),
    .out6(demultiplexer_2_out6), .out7(demultiplexer_2_out7), .in(clock_2_out), .sel(counter_1_q));  // open: en
  Clock clock_2 (.out(clock_2_out));
  Register register_1 (
    .D(demultiplexer_1_out0), .en(in_12), .Q(out_13), .clk(demultiplexer_2_out0), .clr(button_1_out));
  Register register_2 (
    .D(demultiplexer_1_out1), .en(in_12), .Q(out_14), .clk(demultiplexer_2_out1), .clr(button_1_out));
  Register register_3 (
    .D(demultiplexer_1_out2), .en(in_12), .Q(out_15), .clk(demultiplexer_2_out2), .clr(button_1_out));
  Register register_4 (
    .D(demultiplexer_1_out3), .en(in_12), .Q(out_16), .clk(demultiplexer_2_out3), .clr(button_1_out));
  Register register_5 (
    .D(demultiplexer_1_out4), .en(in_12), .Q(out_17), .clk(demultiplexer_2_out4), .clr(button_1_out));
  Register register_6 (
    .D(demultiplexer_1_out5), .en(in_12), .Q(out_18), .clk(demultiplexer_2_out5), .clr(button_1_out));
  Register register_7 (
    .D(demultiplexer_1_out6), .en(in_12), .Q(out_19), .clk(demultiplexer_2_out6), .clr(button_1_out));
  Register register_8 (
    .D(demultiplexer_1_out7), .en(in_12), .Q(out_20), .clk(demultiplexer_2_out7), .clr(button_1_out));

  // Notes on the sheet:
  //   Reset
endmodule

module Joystick (
  output [1:0] out_1,
  output [1:0] out_2,
  output [15:0] out_3
);

  wire and_1_out, and_2_out, and_3_out, and_4_out, button_1_out, clock_1_out, clock_2_out,
       controlled_buffer_1_out, controlled_buffer_2_out, controlled_buffer_3_out, controlled_buffer_4_out,
       not_1_out, not_2_out, or_1_out, or_2_out;
  wire [3:0] counter_1_q, counter_2_q;
  wire [15:0] demultiplexer_1_out0, demultiplexer_1_out1, demultiplexer_1_out2, demultiplexer_1_out3,
       demultiplexer_1_out4, demultiplexer_1_out5, demultiplexer_1_out6, demultiplexer_1_out7,
       demultiplexer_1_out8, demultiplexer_1_out9, demultiplexer_1_out10, demultiplexer_1_out11,
       demultiplexer_1_out12, demultiplexer_1_out13, demultiplexer_1_out14, demultiplexer_1_out15;

  Joystick_part #(.bits(2)) joystick_1 (.x(out_1), .y(out_2));
  not not_1 (not_1_out, out_2[1]);
  not not_2 (not_2_out, out_1[1]);
  Clock clock_1 (.out(clock_1_out));
  and and_1 (and_1_out, out_1[0], out_1[1]);
  and and_2 (and_2_out, out_1[0], not_2_out);
  Clock clock_2 (.out(clock_2_out));
  and and_3 (and_3_out, out_2[0], out_2[1]);
  and and_4 (and_4_out, out_2[0], not_1_out);
  assign controlled_buffer_1_out = and_1_out ? clock_1_out : 1'bz;  // Controlled_Buffer controlled_buffer_1
  assign controlled_buffer_2_out = or_1_out ? clock_1_out : 1'bz;  // Controlled_Buffer controlled_buffer_2
  or or_1 (or_1_out, and_1_out, and_2_out);
  assign controlled_buffer_3_out = and_4_out ? clock_2_out : 1'bz;  // Controlled_Buffer controlled_buffer_3
  assign controlled_buffer_4_out = or_2_out ? clock_2_out : 1'bz;  // Controlled_Buffer controlled_buffer_4
  or or_2 (or_2_out, and_3_out, and_4_out);
  Counter #(.width(4), .max('hf), .ongoal("stay")) counter_1 (
    .load(controlled_buffer_1_out), .D(counter_1_q), .count(controlled_buffer_2_out), .Q(counter_1_q),
    .clk(controlled_buffer_2_out), .clr(button_1_out));  // open: carry
  Counter #(.width(4), .max('hf), .ongoal("stay")) counter_2 (
    .load(controlled_buffer_3_out), .D(counter_2_q), .count(controlled_buffer_4_out), .Q(counter_2_q),
    .clk(controlled_buffer_4_out), .clr(button_1_out));  // open: carry
  Button button_1 (.out(button_1_out));
  Decoder #(.select(4)) decoder_1 (
    .out0(out_3[0]), .out1(out_3[1]), .out2(out_3[2]), .out3(out_3[3]), .out4(out_3[4]), .out5(out_3[5]),
    .out6(out_3[6]), .out7(out_3[7]), .out8(out_3[8]), .out9(out_3[9]), .out10(out_3[10]), .out11(out_3[11]),
    .out12(out_3[12]), .out13(out_3[13]), .out14(out_3[14]), .out15(out_3[15]), .sel(counter_1_q));  // open: en
  Demultiplexer #(.select(4), .width(16)) demultiplexer_1 (
    .out0(demultiplexer_1_out0), .out1(demultiplexer_1_out1), .out2(demultiplexer_1_out2),
    .out3(demultiplexer_1_out3), .out4(demultiplexer_1_out4), .out5(demultiplexer_1_out5),
    .out6(demultiplexer_1_out6), .out7(demultiplexer_1_out7), .out8(demultiplexer_1_out8),
    .out9(demultiplexer_1_out9), .out10(demultiplexer_1_out10), .out11(demultiplexer_1_out11),
    .out12(demultiplexer_1_out12), .out13(demultiplexer_1_out13), .out14(demultiplexer_1_out14),
    .out15(demultiplexer_1_out15), .in(out_3), .sel(counter_2_q));  // open: en
  DotMatrix #(.inputtype("row"), .matrixcols(16), .matrixrows(16)) dotmatrix_1 (
    .row0(demultiplexer_1_out0), .row1(demultiplexer_1_out1), .row2(demultiplexer_1_out2),
    .row3(demultiplexer_1_out3), .row4(demultiplexer_1_out4), .row5(demultiplexer_1_out5),
    .row6(demultiplexer_1_out6), .row7(demultiplexer_1_out7), .row8(demultiplexer_1_out8),
    .row9(demultiplexer_1_out9), .row10(demultiplexer_1_out10), .row11(demultiplexer_1_out11),
    .row12(demultiplexer_1_out12), .row13(demultiplexer_1_out13), .row14(demultiplexer_1_out14),
    .row15(demultiplexer_1_out15));
endmodule

module Decodificador (
  input  x,
  input  y,
  input  z,
  output a,
  output b,
  output c,
  output d,
  output e,
  output f,
  output g,
  output h
);

  wire not_1_out, not_2_out, not_3_out, not_4_out, not_5_out, not_6_out, not_7_out, not_8_out, not_9_out,
       not_10_out, not_11_out, not_12_out;

  not not_1 (not_1_out, x);
  not not_2 (not_2_out, y);
  not not_3 (not_3_out, z);
  not not_4 (not_4_out, x);
  not not_5 (not_5_out, y);
  not not_6 (not_6_out, x);
  not not_7 (not_7_out, z);
  not not_8 (not_8_out, x);
  not not_9 (not_9_out, y);
  not not_10 (not_10_out, z);
  not not_11 (not_11_out, y);
  not not_12 (not_12_out, z);
  and and_1 (a, not_1_out, not_2_out, not_3_out);
  and and_2 (b, not_4_out, not_5_out, z);
  and and_3 (c, not_6_out, y, not_7_out);
  and and_4 (d, not_8_out, y, z);
  and and_5 (e, x, not_9_out, not_10_out);
  and and_6 (f, x, not_11_out, z);
  and and_7 (g, x, y, not_12_out);
  and and_8 (h, x, y, z);
endmodule

module \Memória_Posição  (
);

  Register register_1 ();  // open: D, en, Q, clk, clr
endmodule

module Somador (
  input  [15:0] in_1,
  input  [15:0] in_2,
  input  [15:0] in_3,
  input  [15:0] in_4,
  input  [15:0] in_5,
  input  [15:0] in_6,
  input  [15:0] in_7,
  input  [15:0] in_8,
  input  [15:0] in_9,
  input  [15:0] in_10,
  input  [15:0] in_11,
  input  [15:0] in_12,
  input  [15:0] in_13,
  input  [15:0] in_14,
  input  [15:0] in_15,
  input  [15:0] in_16,
  input  [15:0] in_17,
  input  [15:0] in_18,
  input  [15:0] in_19,
  input  [15:0] in_20,
  input  [15:0] in_21,
  input  [15:0] in_22,
  input  [15:0] in_23,
  input  [15:0] in_24,
  input  [15:0] in_25,
  input  [15:0] in_26,
  input  [15:0] in_27,
  input  [15:0] in_28,
  input  [15:0] in_29,
  input  [15:0] in_30,
  input  [15:0] in_31,
  input  [15:0] in_32,
  output [15:0] out_33,
  output [15:0] out_34,
  output [15:0] out_35,
  output [15:0] out_36,
  output [15:0] out_37,
  output [15:0] out_38,
  output [15:0] out_39,
  output [15:0] out_40,
  output [15:0] out_41,
  output [15:0] out_42,
  output [15:0] out_43,
  output [15:0] out_44,
  output [15:0] out_45,
  output [15:0] out_46,
  output [15:0] out_47,
  output [15:0] out_48
);

  Adder #(.width(16)) adder_1 (.a(in_1), .b(in_2), .out(out_33));  // open: cin, cout
  Adder #(.width(16)) adder_2 (.a(in_3), .b(in_4), .out(out_34));  // open: cin, cout
  Adder #(.width(16)) adder_3 (.a(in_5), .b(in_6), .out(out_35));  // open: cin, cout
  Adder #(.width(16)) adder_4 (.a(in_7), .b(in_8), .out(out_36));  // open: cin, cout
  Adder #(.width(16)) adder_5 (.a(in_9), .b(in_10), .out(out_37));  // open: cin, cout
  Adder #(.width(16)) adder_6 (.a(in_11), .b(in_12), .out(out_38));  // open: cin, cout
  Adder #(.width(16)) adder_7 (.a(in_13), .b(in_14), .out(out_39));  // open: cin, cout
  Adder #(.width(16)) adder_8 (.a(in_15), .b(in_16), .out(out_40));  // open: cin, cout
  Adder #(.width(16)) adder_9 (.a(in_17), .b(in_18), .out(out_41));  // open: cin, cout
  Adder #(.width(16)) adder_10 (.a(in_19), .b(in_20), .out(out_42));  // open: cin, cout
  Adder #(.width(16)) adder_11 (.a(in_21), .b(in_22), .out(out_43));  // open: cin, cout
  Adder #(.width(16)) adder_12 (.a(in_23), .b(in_24), .out(out_44));  // open: cin, cout
  Adder #(.width(16)) adder_13 (.a(in_25), .b(in_26), .out(out_45));  // open: cin, cout
  Adder #(.width(16)) adder_14 (.a(in_27), .b(in_28), .out(out_46));  // open: cin, cout
  Adder #(.width(16)) adder_15 (.a(in_29), .b(in_30), .out(out_47));  // open: cin, cout
  Adder #(.width(16)) adder_16 (.a(in_31), .b(in_32), .out(out_48));  // open: cin, cout
endmodule

module Comparador (
  input  [15:0] in_1,
  input  [15:0] in_2,
  input  [15:0] in_3,
  input  [15:0] in_4,
  input  [15:0] in_5,
  input  [15:0] in_6,
  input  [15:0] in_7,
  input  [15:0] in_8,
  input  [15:0] in_9,
  input  [15:0] in_10,
  input  [15:0] in_11,
  input  [15:0] in_12,
  input  [15:0] in_13,
  input  [15:0] in_14,
  input  [15:0] in_15,
  input  [15:0] in_16,
  input  [15:0] in_17,
  input  [15:0] in_18,
  input  [15:0] in_19,
  input  [15:0] in_20,
  input  [15:0] in_21,
  input  [15:0] in_22,
  input  [15:0] in_23,
  input  [15:0] in_24,
  input  [15:0] in_25,
  input  [15:0] in_26,
  input  [15:0] in_27,
  input  [15:0] in_28,
  input  [15:0] in_29,
  input  [15:0] in_30,
  input  [15:0] in_31,
  input  [15:0] in_32,
  input  [3:0] in_33,
  output [15:0] out_34,
  output [15:0] out_35,
  output [15:0] out_36,
  output [15:0] out_37,
  output [15:0] out_38,
  output [15:0] out_39,
  output [15:0] out_40,
  output [15:0] out_41,
  output [15:0] out_42,
  output [15:0] out_43,
  output [15:0] out_44,
  output [15:0] out_45,
  output [15:0] out_46,
  output [15:0] out_47,
  output [15:0] out_48,
  output [15:0] out_49,
  output [15:0] out_50,
  output [15:0] out_51,
  output [15:0] out_52,
  output [15:0] out_53,
  output [15:0] out_54,
  output [15:0] out_55,
  output [15:0] out_56,
  output [15:0] out_57,
  output [15:0] out_58,
  output [15:0] out_59,
  output [15:0] out_60,
  output [15:0] out_61,
  output [15:0] out_62,
  output [15:0] out_63,
  output [15:0] out_64,
  output [15:0] out_65,
  output out_66
);

  wire and_1_out, and_2_out, and_3_out, and_4_out, and_5_out, and_6_out, and_7_out, and_8_out, and_9_out,
       and_10_out, and_11_out, and_12_out, and_13_out, and_14_out, and_15_out, and_16_out, not_1_out,
       not_2_out, not_3_out, not_4_out, not_5_out, not_6_out, not_7_out, not_8_out, not_9_out, not_10_out,
       not_11_out, not_12_out, not_13_out, not_14_out, not_15_out, not_16_out, not_17_out, not_18_out,
       not_19_out, not_20_out, not_21_out, not_22_out, not_23_out, not_24_out, not_25_out, not_26_out,
       not_27_out, not_28_out, not_29_out, not_30_out, not_31_out, not_32_out;
  wire [15:0] controlled_buffer_1_out, controlled_buffer_2_out;

  not not_1 (not_1_out, in_33[1]);
  not not_2 (not_2_out, in_33[0]);
  assign controlled_buffer_1_out = and_2_out ? in_1 : 16'bz;  // Controlled_Buffer controlled_buffer_1
  assign controlled_buffer_2_out = and_2_out ? in_2 : 16'bz;  // Controlled_Buffer controlled_buffer_2
  assign controlled_buffer_1_out = and_1_out ? in_3 : 16'bz;  // Controlled_Buffer controlled_buffer_3
  assign controlled_buffer_2_out = and_1_out ? in_4 : 16'bz;  // Controlled_Buffer controlled_buffer_4
  and and_1 (and_1_out, in_33[0], not_6_out, not_3_out, not_9_out);
  and and_2 (and_2_out, not_2_out, not_1_out, not_5_out, not_4_out);
  not not_3 (not_3_out, in_33[2]);
  not not_4 (not_4_out, in_33[3]);
  not not_5 (not_5_out, in_33[2]);
  not not_6 (not_6_out, in_33[1]);
  assign controlled_buffer_1_out = and_3_out ? in_5 : 16'bz;  // Controlled_Buffer controlled_buffer_5
  assign controlled_buffer_2_out = and_3_out ? in_6 : 16'bz;  // Controlled_Buffer controlled_buffer_6
  assign controlled_buffer_1_out = and_4_out ? in_7 : 16'bz;  // Controlled_Buffer controlled_buffer_7
  assign controlled_buffer_2_out = and_4_out ? in_8 : 16'bz;  // Controlled_Buffer controlled_buffer_8
  and and_3 (and_3_out, not_8_out, in_33[1], not_7_out, not_10_out);
  not not_7 (not_7_out, in_33[2]);
  not not_8 (not_8_out, in_33[0]);
  not not_9 (not_9_out, in_33[3]);
  not not_10 (not_10_out, in_33[3]);
  assign controlled_buffer_1_out = and_6_out ? in_9 : 16'bz;  // Controlled_Buffer controlled_buffer_9
  assign controlled_buffer_2_out = and_6_out ? in_10 : 16'bz;  // Controlled_Buffer controlled_buffer_10
  assign controlled_buffer_1_out = and_5_out ? in_11 : 16'bz;  // Controlled_Buffer controlled_buffer_11
  assign controlled_buffer_2_out = and_5_out ? in_12 : 16'bz;  // Controlled_Buffer controlled_buffer_12
  and and_4 (and_4_out, in_33[0], in_33[1], not_14_out, not_13_out);
  not not_11 (not_11_out, in_33[1]);
  not not_12 (not_12_out, in_33[0]);
  not not_13 (not_13_out, in_33[3]);
  not not_14 (not_14_out, in_33[2]);
  assign controlled_buffer_1_out = and_7_out ? in_13 : 16'bz;  // Controlled_Buffer controlled_buffer_13
  assign controlled_buffer_2_out = and_7_out ? in_14 : 16'bz;  // Controlled_Buffer controlled_buffer_14
  assign controlled_buffer_1_out = and_8_out ? in_15 : 16'bz;  // Controlled_Buffer controlled_buffer_15
  assign controlled_buffer_2_out = and_8_out ? in_16 : 16'bz;  // Controlled_Buffer controlled_buffer_16
  and and_5 (and_5_out, in_33[0], not_15_out, in_33[2], not_19_out);
  and and_6 (and_6_out, not_12_out, not_11_out, in_33[2], not_16_out);
  not not_15 (not_15_out, in_33[1]);
  not not_16 (not_16_out, in_33[3]);
  assign controlled_buffer_1_out = and_9_out ? in_17 : 16'bz;  // Controlled_Buffer controlled_buffer_17
  assign controlled_buffer_2_out = and_9_out ? in_18 : 16'bz;  // Controlled_Buffer controlled_buffer_18
  assign controlled_buffer_1_out = and_10_out ? in_19 : 16'bz;  // Controlled_Buffer controlled_buffer_19
  assign controlled_buffer_2_out = and_10_out ? in_20 : 16'bz;  // Controlled_Buffer controlled_buffer_20
  and and_7 (and_7_out, not_18_out, in_33[1], in_33[2], not_17_out);
  not not_17 (not_17_out, in_33[3]);
  not not_18 (not_18_out, in_33[0]);
  not not_19 (not_19_out, in_33[3]);
  assign controlled_buffer_1_out = and_11_out ? in_21 : 16'bz;  // Controlled_Buffer controlled_buffer_21
  assign controlled_buffer_2_out = and_11_out ? in_22 : 16'bz;  // Controlled_Buffer controlled_buffer_22
  assign controlled_buffer_1_out = and_12_out ? in_23 : 16'bz;  // Controlled_Buffer controlled_buffer_23
  assign controlled_buffer_2_out = and_12_out ? in_24 : 16'bz;  // Controlled_Buffer controlled_buffer_24
  and and_8 (and_8_out, in_33[0], in_33[1], in_33[2], not_22_out);
  not not_20 (not_20_out, in_33[1]);
  not not_21 (not_21_out, in_33[0]);
  not not_22 (not_22_out, in_33[3]);
  assign controlled_buffer_1_out = and_13_out ? in_25 : 16'bz;  // Controlled_Buffer controlled_buffer_25
  assign controlled_buffer_2_out = and_13_out ? in_26 : 16'bz;  // Controlled_Buffer controlled_buffer_26
  assign controlled_buffer_1_out = and_14_out ? in_27 : 16'bz;  // Controlled_Buffer controlled_buffer_27
  assign controlled_buffer_2_out = and_14_out ? in_28 : 16'bz;  // Controlled_Buffer controlled_buffer_28
  and and_9 (and_9_out, not_21_out, not_20_out, not_25_out, in_33[3]);
  and and_10 (and_10_out, in_33[0], not_24_out, not_23_out, in_33[3]);
  not not_23 (not_23_out, in_33[2]);
  not not_24 (not_24_out, in_33[1]);
  not not_25 (not_25_out, in_33[2]);
  assign controlled_buffer_1_out = and_15_out ? in_29 : 16'bz;  // Controlled_Buffer controlled_buffer_29
  assign controlled_buffer_2_out = and_15_out ? in_30 : 16'bz;  // Controlled_Buffer controlled_buffer_30
  assign controlled_buffer_1_out = and_16_out ? in_31 : 16'bz;  // Controlled_Buffer controlled_buffer_31
  assign controlled_buffer_2_out = and_16_out ? in_32 : 16'bz;  // Controlled_Buffer controlled_buffer_32
  and and_11 (and_11_out, not_26_out, in_33[1], not_27_out, in_33[3]);
  not not_26 (not_26_out, in_33[0]);
  not not_27 (not_27_out, in_33[2]);
  and and_12 (and_12_out, in_33[0], in_33[1], not_28_out, in_33[3]);
  not not_28 (not_28_out, in_33[2]);
  not not_29 (not_29_out, in_33[1]);
  not not_30 (not_30_out, in_33[0]);
  Comparator #(.width(16)) comparator_1 (
    .a(controlled_buffer_1_out), .b(controlled_buffer_2_out), .eq(out_66));  // open: gt, lt
  and and_13 (and_13_out, not_30_out, not_29_out, in_33[2], in_33[3]);
  and and_14 (and_14_out, in_33[0], not_31_out, in_33[2], in_33[3]);
  not not_31 (not_31_out, in_33[1]);
  and and_15 (and_15_out, not_32_out, in_33[1], in_33[2], in_33[3]);
  not not_32 (not_32_out, in_33[0]);
  and and_16 (and_16_out, in_33[0], in_33[1], in_33[2], in_33[3]);

  assign out_34 = in_1;
  assign out_35 = in_2;
  assign out_36 = in_3;
  assign out_37 = in_4;
  assign out_38 = in_5;
  assign out_39 = in_6;
  assign out_40 = in_7;
  assign out_41 = in_8;
  assign out_42 = in_9;
  assign out_43 = in_10;
  assign out_44 = in_11;
  assign out_45 = in_12;
  assign out_46 = in_13;
  assign out_47 = in_14;
  assign out_48 = in_15;
  assign out_49 = in_16;
  assign out_50 = in_17;
  assign out_51 = in_18;
  assign out_52 = in_19;
  assign out_53 = in_20;
  assign out_54 = in_21;
  assign out_55 = in_22;
  assign out_56 = in_23;
  assign out_57 = in_24;
  assign out_58 = in_25;
  assign out_59 = in_26;
  assign out_60 = in_27;
  assign out_61 = in_28;
  assign out_62 = in_29;
  assign out_63 = in_30;
  assign out_64 = in_31;
  assign out_65 = in_32;
endmodule
