// Logisim project Circuitos-M3.circ as structural Verilog: 11 circuits, main circuit main
module main (
  input  _0_Write___1___Load,
  input  Clear,
  output [7:0] out_3
);

  wire clock_1_out, controlled_buffer_1_out, counter_1_carry, not_1_out, not_2_out;
  wire [3:0] counter_1_q;
  wire [7:0] controlled_buffer_2_out, random_1_out;

  Random random_1 (.clk(controlled_buffer_1_out), .out(random_1_out));  // open: next, clr
  Counter #(.width(4), .max('hf)) counter_1 (
    .Q(counter_1_q), .carry(counter_1_carry), .clk(controlled_buffer_1_out));  // open: load, D, count, clr
  not not_1 (not_1_out, counter_1_carry);
  Clock clock_1 (.out(clock_1_out));
  assign controlled_buffer_1_out = not_1_out ? clock_1_out : 1'bz;  // Controlled_Buffer controlled_buffer_1
  assign controlled_buffer_2_out = not_2_out ? random_1_out : 8'bz;  // Controlled_Buffer controlled_buffer_2
  RAM #(.addrWidth(4)) ram_1 (
    .addr(counter_1_q), .data(controlled_buffer_2_out), .clk(controlled_buffer_1_out),
    .ld(_0_Write___1___Load), .clr(Clear));  // open: sel
  not not_2 (not_2_out, _0_Write___1___Load);
  assign out_3 = _0_Write___1___Load ? controlled_buffer_2_out : 8'bz;  // Controlled_Buffer controlled_buffer_3
endmodule

module \Laço_Dependente  (
);

  wire and_1_out, button_1_out, clock_1_out, comparator_1_lt, comparator_2_eq, or_1_out;
  wire [3:0] counter_1_q, counter_2_q;

  Counter #(.width(4), .max('h9)) counter_1 (
    .Q(counter_1_q), .clk(clock_1_out), .clr(and_1_out));  // open: load, D, count, carry
  Clock clock_1 (.out(clock_1_out));
  Button button_1 (.out(button_1_out));
  Comparator #(.width(4), .mode("unsigned")) comparator_1 (
    .a(counter_2_q), .b(counter_1_q), .lt(comparator_1_lt));  // open: gt, eq
  Counter #(.width(4), .max('h9)) counter_2 (
    .Q(counter_2_q), .clk(and_1_out), .clr(or_1_out));  // open: load, D, count, carry
  or or_1 (or_1_out, button_1_out, comparator_2_eq);
  and and_1 (and_1_out, comparator_1_lt, clock_1_out);
  Comparator #(.width(4)) comparator_2 (.a(counter_2_q), .b(4'b0111), .eq(comparator_2_eq));  // open: gt, lt
endmodule

module \Memória  (
  input  Enable,
  input  Clear,
  output Finished,
  output [5:0] \Posição_1 ,
  output [5:0] \Posição_2 ,
  output [5:0] \Posição_3 ,
  output [5:0] \Posição_4 ,
  output [5:0] \Posição_5 ,
  output [5:0] \Posição_6 ,
  output [5:0] \Posição_7 ,
  output [3:0] Carta_1,
  output [3:0] Carta_2,
  output [3:0] Carta_3,
  output [3:0] Carta_4,
  output [3:0] Carta_5,
  output [3:0] Carta_6,
  output [3:0] Carta_7
);

  wire and_1_out, and_2_out, and_3_out, clock_1_out, comparador_geral_1_saida, comparator_1_lt,
       controlled_buffer_1_out, controlled_buffer_4_out, controlled_buffer_6_out, counter_1_carry,
       counter_3_carry, counter_4_carry, counter_5_carry, not_1_out, not_2_out, not_4_out, or_1_out,
       or_2_out, selecionador_1_overflow, \selecionador_posição_1_overflow ;
  wire [3:0] adder_1_out, controlled_buffer_7_out, counter_2_q, selecionador_1__1, selecionador_1__2,
       selecionador_1__3, selecionador_1__4, selecionador_1__5, selecionador_1__6, selecionador_1__7;
  wire [5:0] controlled_buffer_2_out, counter_1_q, random_1_out, \selecionador_posição_1__1 ,
       \selecionador_posição_1__2 , \selecionador_posição_1__3 , \selecionador_posição_1__4 ,
       \selecionador_posição_1__5 , \selecionador_posição_1__6 , \selecionador_posição_1__7 ;

  Clock clock_1 (.out(clock_1_out));
  and and_1 (and_1_out, comparator_1_lt, counter_1_carry);
  assign controlled_buffer_1_out = and_2_out ? clock_1_out : 1'bz;  // Controlled_Buffer controlled_buffer_1
  and and_2 (and_2_out, Enable, not_2_out);
  Comparator #(.width(4), .mode("unsigned")) comparator_1 (
    .a(4'b0000), .b(controlled_buffer_7_out), .lt(comparator_1_lt));  // open: gt, eq
  Counter #(.width(6), .max('h28), .ongoal("stay")) counter_1 (
    .Q(counter_1_q), .carry(counter_1_carry), .clk(controlled_buffer_1_out), .clr(or_1_out));  // open: load, D, count
  not not_1 (not_1_out, counter_1_carry);
  Random #(.width(6)) random_1 (.clk(controlled_buffer_1_out), .out(random_1_out));  // open: next, clr
  assign controlled_buffer_2_out = counter_1_carry ? random_1_out : 6'bz;  // Controlled_Buffer controlled_buffer_2
  not not_2 (not_2_out, counter_5_carry);
  or or_1 (or_1_out, Clear, comparador_geral_1_saida);
  assign controlled_buffer_2_out = not_1_out ? counter_1_q : 6'bz;  // Controlled_Buffer controlled_buffer_3
  assign controlled_buffer_4_out = not_1_out ? controlled_buffer_1_out : 1'bz;  // Controlled_Buffer controlled_buffer_4
  assign controlled_buffer_4_out = and_1_out ? controlled_buffer_1_out : 1'bz;  // Controlled_Buffer controlled_buffer_5
  assign controlled_buffer_6_out = and_1_out ? controlled_buffer_1_out : 1'bz;  // Controlled_Buffer controlled_buffer_6
  assign controlled_buffer_7_out = not_1_out ? adder_1_out : 4'bz;  // Controlled_Buffer controlled_buffer_7
  Counter #(.width(4), .max('ha), .ongoal("stay")) counter_2 (
    .Q(counter_2_q), .clk(counter_3_carry), .clr(or_1_out));  // open: load, D, count, carry
  RAM #(.addrWidth(6), .dataWidth(4)) ram_1 (
    .addr(controlled_buffer_2_out), .data(controlled_buffer_7_out), .clk(controlled_buffer_4_out),
    .ld(counter_1_carry), .clr(or_1_out));  // open: sel
  Adder #(.width(4)) adder_1 (.a(4'b0001), .b(counter_2_q), .out(adder_1_out));  // open: cin, cout
  Counter #(.width(4), .max('h3)) counter_3 (
    .carry(counter_3_carry), .clk(controlled_buffer_4_out), .clr(or_2_out));  // open: load, D, count, Q
  or or_2 (or_2_out, or_1_out, not_4_out);
  Selecionador selecionador_1 (
    .Carta(controlled_buffer_7_out), .Clock(controlled_buffer_6_out), .Clear(or_1_out),
    ._4(selecionador_1__4), ._5(selecionador_1__5), ._6(selecionador_1__6), ._7(selecionador_1__7),
    ._1(selecionador_1__1), ._2(selecionador_1__2), ._3(selecionador_1__3), .Overflow(selecionador_1_overflow));
  \Selecionador_Posição  \selecionador_posição_1  (
    .\Posição (random_1_out), .Clock(controlled_buffer_6_out), .Clear(or_1_out),
    ._4(\selecionador_posição_1__4 ), ._5(\selecionador_posição_1__5 ), ._6(\selecionador_posição_1__6 ),
    ._7(\selecionador_posição_1__7 ), ._1(\selecionador_posição_1__1 ), ._2(\selecionador_posição_1__2 ),
    ._3(\selecionador_posição_1__3 ), .Overflow(\selecionador_posição_1_overflow ));
  not not_3 (Finished, comparador_geral_1_saida);
  Counter #(.width(1), .max('h1), .ongoal("stay")) counter_4 (
    .carry(counter_4_carry), .clk(controlled_buffer_4_out), .clr(or_1_out));  // open: load, D, count, Q
  not not_4 (not_4_out, counter_4_carry);
  Counter #(.width(1), .max('h1)) counter_5 (.load(Finished), .carry(counter_5_carry));  // open: D, count, Q, clk, clr
  and and_3 (and_3_out, selecionador_1_overflow, \selecionador_posição_1_overflow );
  Comparador_Geral comparador_geral_1 (
    ._1(\Posição_1 ), ._2(\Posição_2 ), ._3(\Posição_3 ), ._4(\Posição_4 ), ._5(\Posição_5 ),
    ._6(\Posição_6 ), .Enable(and_3_out), .Saida(comparador_geral_1_saida), ._7(\Posição_7 ));
  Register #(.width(6)) register_1 (
    .D(\selecionador_posição_1__1 ), .Q(\Posição_1 ), .clk(controlled_buffer_6_out), .clr(or_1_out));  // open: en
  Register #(.width(4)) register_2 (
    .D(selecionador_1__1), .Q(Carta_1), .clk(controlled_buffer_6_out), .clr(or_1_out));  // open: en
  Register #(.width(4)) register_3 (
    .D(selecionador_1__4), .Q(Carta_4), .clk(controlled_buffer_6_out), .clr(or_1_out));  // open: en
  Register #(.width(6)) register_4 (
    .D(\selecionador_posição_1__4 ), .Q(\Posição_4 ), .clk(controlled_buffer_6_out), .clr(or_1_out));  // open: en
  Register #(.width(6)) register_5 (
    .D(\selecionador_posição_1__3 ), .Q(\Posição_3 ), .clk(controlled_buffer_6_out), .clr(or_1_out));  // open: en
  Register #(.width(6)) register_6 (
    .D(\selecionador_posição_1__2 ), .Q(\Posição_2 ), .clk(controlled_buffer_6_out), .clr(or_1_out));  // open: en
  Register #(.width(4)) register_7 (
    .D(selecionador_1__2), .Q(Carta_2), .clk(controlled_buffer_6_out), .clr(or_1_out));  // open: en
  Register #(.width(4)) register_8 (
    .D(selecionador_1__3), .Q(Carta_3), .clk(controlled_buffer_6_out), .clr(or_1_out));  // open: en
  Register #(.width(4)) register_9 (
    .D(selecionador_1__6), .Q(Carta_6), .clk(controlled_buffer_6_out), .clr(or_1_out));  // open: en
  Register #(.width(4)) register_10 (
    .D(selecionador_1__5), .Q(Carta_5), .clk(controlled_buffer_6_out), .clr(or_1_out));  // open: en
  Register #(.width(6)) register_11 (
    .D(\selecionador_posição_1__6 ), .Q(\Posição_6 ), .clk(controlled_buffer_6_out), .clr(or_1_out));  // open: en
  Register #(.width(6)) register_12 (
    .D(\selecionador_posição_1__5 ), .Q(\Posição_5 ), .clk(controlled_buffer_6_out), .clr(or_1_out));  // open: en
  Register #(.width(4)) register_13 (
    .D(selecionador_1__7), .Q(Carta_7), .clk(controlled_buffer_6_out), .clr(or_1_out));  // open: en
  Register #(.width(6)) register_14 (
    .D(\selecionador_posição_1__7 ), .Q(\Posição_7 ), .clk(controlled_buffer_6_out), .clr(or_1_out));  // open: en
endmodule

module Truco (
  input  Enable,
  output out_2,
  output out_3
);

  wire button_1_out, button_2_out, button_3_out, button_4_out, Clear_out, clock_2_out, clock_3_out,
       Clock_out, comparador_truco_1_clock_1, comparador_truco_1_clock_2, comparador_truco_1_embuchada,
       comparator_1_eq, comparator_1_gt, comparator_1_lt, controlled_buffer_1_out, controlled_buffer_2_out,
       controlled_buffer_3_out, controlled_buffer_19_out, controlled_buffer_20_out, controlled_buffer_21_out,
       controlled_buffer_22_out, counter_1_carry, counter_2_carry, counter_3_carry, counter_4_carry,
       counter_6_carry, counter_7_carry, counter_8_carry, counter_9_carry, counter_10_carry,
       counter_11_carry, counter_14_carry, \memória_1_finished , not_1_out, not_2_out, not_3_out, not_4_out,
       not_5_out, not_6_out, not_7_out, not_8_out, not_9_out, not_10_out, or_1_out, or_2_out, or_5_out,
       or_6_out, or_7_out, or_8_out, Score_Partida_2_carry, Score_Partida_carry, TRUCO_out;
  wire [1:0] counter_5_q;
  wire [3:0] adder_1_out, adder_2_out, controlled_buffer_4_out, controlled_buffer_6_out,
       controlled_buffer_8_out, controlled_buffer_11_out, controlled_buffer_18_out, counter_12_q,
       counter_13_q, \memória_1_carta_1 , \memória_1_carta_2 , \memória_1_carta_3 , \memória_1_carta_4 ,
       \memória_1_carta_5 , \memória_1_carta_6 , \memória_1_carta_7 , register_2_q, register_3_q,
       register_6_q, register_8_q, register_9_q, register_12_q, register_13_q;
  wire [5:0] controlled_buffer_5_out, controlled_buffer_7_out, \memória_1_posição_1 , \memória_1_posição_2 ,
       \memória_1_posição_3 , \memória_1_posição_4 , \memória_1_posição_5 , \memória_1_posição_6 ,
       \memória_1_posição_7 , register_1_q, register_4_q, register_5_q, register_10_q, register_11_q,
       register_14_q;

  Counter #(.width(1), .max('h1)) counter_1 (
    .carry(counter_1_carry), .clk(controlled_buffer_1_out), .clr(or_2_out));  // open: load, D, count, Q
  not not_1 (not_1_out, counter_2_carry);
  not not_2 (not_2_out, counter_1_carry);
  not not_3 (not_3_out, counter_4_carry);
  or or_1 (or_1_out, controlled_buffer_1_out, controlled_buffer_3_out, controlled_buffer_2_out);
  assign controlled_buffer_1_out = not_2_out ? button_3_out : 1'bz;  // Controlled_Buffer controlled_buffer_1
  assign controlled_buffer_2_out = not_3_out ? button_1_out : 1'bz;  // Controlled_Buffer controlled_buffer_2
  assign controlled_buffer_3_out = not_1_out ? button_2_out : 1'bz;  // Controlled_Buffer controlled_buffer_3
  Counter #(.width(1), .max('h1)) counter_2 (
    .carry(counter_2_carry), .clk(controlled_buffer_3_out), .clr(or_2_out));  // open: load, D, count, Q
  Counter #(.width(1), .max('h1)) counter_3 (
    .load(\memória_1_finished ), .carry(counter_3_carry));  // open: D, count, Q, clk, clr
  Clock Clock (.out(Clock_out));
  Button Clear (.out(Clear_out));
  Counter #(.width(1), .max('h1)) counter_4 (
    .carry(counter_4_carry), .clk(controlled_buffer_2_out), .clr(or_2_out));  // open: load, D, count, Q
  Counter #(.width(2), .max('h2)) counter_5 (
    .Q(counter_5_q), .clk(or_1_out), .clr(or_2_out));  // open: load, D, count, carry
  \Memória  \memória_1  (
    .Finished(\memória_1_finished ), .Enable(Enable), .Clear(or_2_out), .\Posição_1 (\memória_1_posição_1 ),
    .\Posição_2 (\memória_1_posição_2 ), .\Posição_3 (\memória_1_posição_3 ),
    .\Posição_4 (\memória_1_posição_4 ), .\Posição_5 (\memória_1_posição_5 ),
    .\Posição_6 (\memória_1_posição_6 ), .\Posição_7 (\memória_1_posição_7 ), .Carta_1(\memória_1_carta_1 ),
    .Carta_2(\memória_1_carta_2 ), .Carta_3(\memória_1_carta_3 ), .Carta_4(\memória_1_carta_4 ),
    .Carta_5(\memória_1_carta_5 ), .Carta_6(\memória_1_carta_6 ), .Carta_7(\memória_1_carta_7 ));
  Comparator #(.width(2), .mode("unsigned")) comparator_1 (
    .a(2'b01), .b(counter_5_q), .gt(comparator_1_gt), .eq(comparator_1_eq), .lt(comparator_1_lt));
  Register #(.width(6)) register_1 (
    .D(\memória_1_posição_1 ), .Q(register_1_q), .clk(counter_3_carry));  // open: en, clr
  Register #(.width(4)) register_2 (.D(\memória_1_carta_1 ), .Q(register_2_q), .clk(counter_3_carry));  // open: en, clr
  Register #(.width(4)) register_3 (.D(\memória_1_carta_4 ), .Q(register_3_q), .clk(counter_3_carry));  // open: en, clr
  Register #(.width(6)) register_4 (
    .D(\memória_1_posição_4 ), .Q(register_4_q), .clk(counter_3_carry));  // open: en, clr
  Counter #(.width(2), .max('h1), .ongoal("stay")) counter_6 (
    .carry(counter_6_carry), .clk(button_1_out), .clr(or_2_out));  // open: load, D, count, Q
  assign controlled_buffer_4_out = comparator_1_lt ? register_2_q : 4'bz;  // Controlled_Buffer controlled_buffer_4
  assign controlled_buffer_5_out = comparator_1_lt ? register_1_q : 6'bz;  // Controlled_Buffer controlled_buffer_5
  assign controlled_buffer_6_out = button_1_out ? register_3_q : 4'bz;  // Controlled_Buffer controlled_buffer_6
  Button button_1 (.out(button_1_out));
  assign controlled_buffer_7_out = button_1_out ? register_4_q : 6'bz;  // Controlled_Buffer controlled_buffer_7
  assign controlled_buffer_8_out = not_4_out ? controlled_buffer_6_out : 4'bz;  // Controlled_Buffer controlled_buffer_8
  not not_4 (not_4_out, counter_6_carry);
  assign controlled_buffer_4_out = comparator_1_eq ? register_6_q : 4'bz;  // Controlled_Buffer controlled_buffer_9
  Register #(.width(6)) register_5 (
    .D(\memória_1_posição_2 ), .Q(register_5_q), .clk(counter_3_carry));  // open: en, clr
  assign controlled_buffer_5_out = comparator_1_eq ? register_5_q : 6'bz;  // Controlled_Buffer controlled_buffer_10
  Register #(.width(4)) register_6 (.D(\memória_1_carta_2 ), .Q(register_6_q), .clk(counter_3_carry));  // open: en, clr
  Register #(.width(6)) register_7 (.D(\memória_1_posição_7 ), .clk(counter_3_carry));  // open: en, Q, clr
  Register #(.width(4)) register_8 (.D(\memória_1_carta_7 ), .Q(register_8_q), .clk(counter_3_carry));  // open: en, clr
  assign controlled_buffer_11_out = button_2_out ? register_9_q : 4'bz;  // Controlled_Buffer controlled_buffer_11
  Button button_2 (.out(button_2_out));
  Register #(.width(4)) register_9 (.D(\memória_1_carta_5 ), .Q(register_9_q), .clk(counter_3_carry));  // open: en, clr
  Register #(.width(6)) register_10 (
    .D(\memória_1_posição_5 ), .Q(register_10_q), .clk(counter_3_carry));  // open: en, clr
  assign controlled_buffer_7_out = button_2_out ? register_10_q : 6'bz;  // Controlled_Buffer controlled_buffer_12
  Counter #(.width(2), .max('h1), .ongoal("stay")) counter_7 (
    .carry(counter_7_carry), .clk(button_2_out), .clr(or_2_out));  // open: load, D, count, Q
  Register #(.width(6)) register_11 (
    .D(\memória_1_posição_3 ), .Q(register_11_q), .clk(counter_3_carry));  // open: en, clr
  Register #(.width(4)) register_12 (
    .D(\memória_1_carta_3 ), .Q(register_12_q), .clk(counter_3_carry));  // open: en, clr
  assign controlled_buffer_8_out = not_5_out ? controlled_buffer_11_out : 4'bz;  // Controlled_Buffer controlled_buffer_13
  not not_5 (not_5_out, counter_7_carry);
  or or_2 (or_2_out, Clear_out, or_7_out);
  assign controlled_buffer_4_out = comparator_1_gt ? register_12_q : 4'bz;  // Controlled_Buffer controlled_buffer_14
  assign controlled_buffer_5_out = comparator_1_gt ? register_11_q : 6'bz;  // Controlled_Buffer controlled_buffer_15
  Register #(.width(4)) register_13 (
    .D(\memória_1_carta_6 ), .Q(register_13_q), .clk(counter_3_carry));  // open: en, clr
  Register #(.width(6)) register_14 (
    .D(\memória_1_posição_6 ), .Q(register_14_q), .clk(counter_3_carry));  // open: en, clr
  assign controlled_buffer_7_out = button_3_out ? register_14_q : 6'bz;  // Controlled_Buffer controlled_buffer_16
  Counter #(.width(2), .max('h1), .ongoal("stay")) counter_8 (
    .carry(counter_8_carry), .clk(button_3_out), .clr(or_2_out));  // open: load, D, count, Q
  // OR_Gate or_3 has open pins: in0=comparador_truco_1_clock_2, in1=comparador_truco_1_embuchada, in2=comparador_truco_1_clock_1, out=open
  Comparador_Truco comparador_truco_1 (
    .Clock_1(comparador_truco_1_clock_1), .Carta_1(controlled_buffer_4_out),
    .\Posição_1 (controlled_buffer_5_out), .Coringa_Carta(register_8_q), .Carta_2(controlled_buffer_8_out),
    .\Posição_2 (controlled_buffer_7_out), .Clock_2(comparador_truco_1_clock_2),
    .Embuchada(comparador_truco_1_embuchada));
  assign controlled_buffer_8_out = not_6_out ? controlled_buffer_18_out : 4'bz;  // Controlled_Buffer controlled_buffer_17
  // OR_Gate or_4 has open pins: in0=comparador_truco_1_clock_2, in1=comparador_truco_1_embuchada, in2=comparador_truco_1_clock_1, out=open
  assign controlled_buffer_18_out = button_3_out ? register_13_q : 4'bz;  // Controlled_Buffer controlled_buffer_18
  Button button_3 (.out(button_3_out));
  not not_6 (not_6_out, counter_8_carry);
  Clock clock_2 (.out(clock_2_out));
  assign controlled_buffer_19_out = not_7_out ? clock_2_out : 1'bz;  // Controlled_Buffer controlled_buffer_19
  not not_7 (not_7_out, counter_3_carry);
  Counter #(.width(2), .max('h2)) Score_Partida (
    .carry(Score_Partida_carry), .clk(or_5_out), .clr(controlled_buffer_19_out));  // open: load, D, count, Q
  or or_5 (or_5_out, counter_10_carry, counter_9_carry);
  Counter #(.width(1), .max('h1)) counter_9 (
    .load(comparador_truco_1_clock_1), .carry(counter_9_carry));  // open: D, count, Q, clk, clr
  Counter #(.width(1), .max('h1)) counter_10 (
    .load(comparador_truco_1_embuchada), .carry(counter_10_carry));  // open: D, count, Q, clk, clr
  Counter #(.width(1), .max('h1)) counter_11 (
    .load(comparador_truco_1_clock_2), .carry(counter_11_carry));  // open: D, count, Q, clk, clr
  or or_6 (or_6_out, counter_10_carry, counter_11_carry);
  Counter #(.width(2), .max('h2)) Score_Partida_2 (
    .carry(Score_Partida_2_carry), .clk(or_6_out), .clr(controlled_buffer_20_out));  // open: load, D, count, Q
  assign controlled_buffer_20_out = not_8_out ? clock_3_out : 1'bz;  // Controlled_Buffer controlled_buffer_20
  not not_8 (not_8_out, counter_3_carry);
  Clock clock_3 (.out(clock_3_out));
  not not_9 (not_9_out, counter_14_carry);
  Counter #(.width(4), .max('hc)) counter_12 (
    .load(counter_14_carry), .D(adder_1_out), .count(not_9_out), .Q(counter_12_q), .carry(out_2),
    .clk(controlled_buffer_21_out), .clr(button_4_out));
  assign controlled_buffer_21_out = counter_3_carry ? Score_Partida_carry : 1'bz;  // Controlled_Buffer controlled_buffer_21
  Button button_4 (.out(button_4_out));
  not not_10 (not_10_out, counter_14_carry);
  Counter #(.width(4), .max('hc)) counter_13 (
    .load(counter_14_carry), .D(adder_2_out), .count(not_10_out), .Q(counter_13_q), .carry(out_3),
    .clk(controlled_buffer_22_out), .clr(button_4_out));
  assign controlled_buffer_22_out = counter_3_carry ? Score_Partida_2_carry : 1'bz;  // Controlled_Buffer controlled_buffer_22
  or or_7 (or_7_out, Score_Partida_2_carry, Score_Partida_carry);
  Adder #(.width(4)) adder_1 (.a(4'b0011), .b(counter_12_q), .out(adder_1_out));  // open: cin, cout
  Counter #(.width(1), .max('h1), .ongoal("stay")) counter_14 (
    .carry(counter_14_carry), .clk(TRUCO_out), .clr(or_8_out));  // open: load, D, count, Q
  or or_8 (or_8_out, controlled_buffer_21_out, controlled_buffer_22_out);
  Button TRUCO (.out(TRUCO_out));
  Adder #(.width(4)) adder_2 (.a(4'b0011), .b(counter_13_q), .out(adder_2_out));  // open: cin, cout
endmodule

module Selecionador (
  input  [3:0] Carta,
  input  Clock,
  input  Clear,
  output [3:0] _4,
  output [3:0] _5,
  output [3:0] _6,
  output [3:0] _7,
  output [3:0] _1,
  output [3:0] _2,
  output [3:0] _3,
  output Overflow
);

  wire and_1_out, and_2_out, and_3_out, and_4_out, and_5_out, and_6_out, and_7_out, controlled_buffer_1_out,
       not_1_out, not_2_out, not_3_out, not_4_out, not_5_out, not_6_out, not_7_out, not_8_out, not_9_out,
       not_10_out, not_11_out, not_12_out, not_13_out;
  wire [2:0] counter_1_q;

  assign controlled_buffer_1_out = not_1_out ? Clock : 1'bz;  // Controlled_Buffer controlled_buffer_1
  Counter #(.width(3), .max('h7), .ongoal("stay")) counter_1 (
    .Q(counter_1_q), .carry(Overflow), .clk(controlled_buffer_1_out), .clr(Clear));  // open: load, D, count
  not not_1 (not_1_out, Overflow);
  and and_1 (and_1_out, not_2_out, not_4_out, not_3_out);
  not not_2 (not_2_out, counter_1_q[0]);
  not not_3 (not_3_out, counter_1_q[2]);
  not not_4 (not_4_out, counter_1_q[1]);
  and and_2 (and_2_out, counter_1_q[0], not_5_out, not_6_out);
  not not_5 (not_5_out, counter_1_q[1]);
  not not_6 (not_6_out, counter_1_q[2]);
  assign _4 = and_4_out ? Carta : 4'bz;  // Controlled_Buffer controlled_buffer_2
  assign _1 = and_1_out ? Carta : 4'bz;  // Controlled_Buffer controlled_buffer_3
  and and_3 (and_3_out, not_8_out, counter_1_q[1], not_7_out);
  not not_7 (not_7_out, counter_1_q[2]);
  not not_8 (not_8_out, counter_1_q[0]);
  and and_4 (and_4_out, counter_1_q[0], counter_1_q[1], not_9_out);
  not not_9 (not_9_out, counter_1_q[2]);
  not not_10 (not_10_out, counter_1_q[0]);
  assign _5 = and_5_out ? Carta : 4'bz;  // Controlled_Buffer controlled_buffer_4
  assign _2 = and_2_out ? Carta : 4'bz;  // Controlled_Buffer controlled_buffer_5
  and and_5 (and_5_out, not_10_out, not_12_out, counter_1_q[2]);
  and and_6 (and_6_out, counter_1_q[0], not_11_out, counter_1_q[2]);
  not not_11 (not_11_out, counter_1_q[1]);
  not not_12 (not_12_out, counter_1_q[1]);
  assign _6 = and_6_out ? Carta : 4'bz;  // Controlled_Buffer controlled_buffer_6
  assign _3 = and_3_out ? Carta : 4'bz;  // Controlled_Buffer controlled_buffer_7
  and and_7 (and_7_out, not_13_out, counter_1_q[1], counter_1_q[2]);
  not not_13 (not_13_out, counter_1_q[0]);
  assign _7 = and_7_out ? Carta : 4'bz;  // Controlled_Buffer controlled_buffer_8
endmodule

module \Geração_de_Baralho  (
  input  Enable,
  input  in_2,
  output [5:0] out_3
);

  wire and_1_out, clock_1_out, controlled_buffer_1_out, counter_2_carry, counter_3_carry, counter_4_carry,
       not_1_out, not_2_out;
  wire [3:0] adder_1_out, counter_2_q;

  Clock clock_1 (.out(clock_1_out));
  Counter #(.width(6), .max('h27), .ongoal("stay")) counter_1 (
    .Q(out_3), .clk(controlled_buffer_1_out), .clr(in_2));  // open: load, D, count, carry
  assign controlled_buffer_1_out = and_1_out ? clock_1_out : 1'bz;  // Controlled_Buffer controlled_buffer_1
  and and_1 (and_1_out, Enable, not_1_out);
  not not_1 (not_1_out, counter_2_carry);
  Adder #(.width(4)) adder_1 (.a(4'b0001), .b(counter_2_q), .out(adder_1_out));  // open: cin, cout
  RAM #(.addrWidth(6), .dataWidth(4)) ram_1 (
    .addr(out_3), .data(adder_1_out), .clk(controlled_buffer_1_out), .ld(counter_2_carry), .clr(in_2));  // open: sel
  Counter #(.width(4), .max('ha)) counter_2 (
    .Q(counter_2_q), .carry(counter_2_carry), .clk(counter_4_carry), .clr(in_2));  // open: load, D, count
  Counter #(.width(1), .max('h1), .ongoal("stay")) counter_3 (
    .carry(counter_3_carry), .clk(controlled_buffer_1_out), .clr(in_2));  // open: load, D, count, Q
  Counter #(.width(4), .max('h3)) counter_4 (
    .carry(counter_4_carry), .clk(controlled_buffer_1_out), .clr(not_2_out));  // open: load, D, count, Q
  not not_2 (not_2_out, counter_3_carry);
endmodule

module \Distribuição_de_Cartas  (
  input  [3:0] in_1,
  input  in_2,
  input  in_3,
  output [3:0] out_4,
  output [3:0] out_5,
  output [2:0] out_6
);

  wire clock_1_out, comparator_1_gt, controlled_buffer_1_out;
  wire [3:0] selecionador_1_p6, selecionador_1_p7, selecionador_1_p8, selecionador_1_p9, selecionador_1_p10,
       selecionador_1_p11, selecionador_1_p12;
  wire [5:0] random_1_out;

  Clock clock_1 (.out(clock_1_out));
  Random #(.width(6), .seed(27)) random_1 (.clk(clock_1_out), .out(random_1_out));  // open: next, clr
  Comparator #(.width(6), .mode("unsigned")) comparator_1 (
    .a(6'b101000), .b(random_1_out), .gt(comparator_1_gt));  // open: eq, lt
  RAM #(.addrWidth(6), .dataWidth(4)) ram_1 (
    .addr(random_1_out), .data(out_4), .clk(clock_1_out), .ld(in_2));  // open: sel, clr
  assign controlled_buffer_1_out = comparator_1_gt ? clock_1_out : 1'bz;  // Controlled_Buffer controlled_buffer_1
  // Selecionador selecionador_1: pin names not known; wires that end beside it: out_4, out_6, out_5, controlled_buffer_1_out, in_3, selecionador_1_p6, selecionador_1_p7, selecionador_1_p8, selecionador_1_p9, selecionador_1_p10, selecionador_1_p11, selecionador_1_p12
  Register #(.width(4)) register_1 (.D(selecionador_1_p6), .clk(controlled_buffer_1_out), .clr(in_3));  // open: en, Q
  Register #(.width(4)) register_2 (.D(selecionador_1_p7), .clk(controlled_buffer_1_out), .clr(in_3));  // open: en, Q
  Register #(.width(4)) register_3 (.D(selecionador_1_p10), .clk(controlled_buffer_1_out), .clr(in_3));  // open: en, Q
  Register #(.width(4)) register_4 (.D(selecionador_1_p9), .clk(controlled_buffer_1_out), .clr(in_3));  // open: en, Q
  Register #(.width(4)) register_5 (.D(selecionador_1_p8), .clk(controlled_buffer_1_out), .clr(in_3));  // open: en, Q
  Register #(.width(4)) register_6 (.D(selecionador_1_p11), .clk(controlled_buffer_1_out), .clr(in_3));  // open: en, Q
  Register #(.width(4)) register_7 (.D(selecionador_1_p12), .clk(controlled_buffer_1_out), .clr(in_3));  // open: en, Q
endmodule

module \Selecionador_Posição  (
  input  [5:0] \Posição ,
  input  Clock,
  input  Clear,
  output [5:0] _4,
  output [5:0] _5,
  output [5:0] _6,
  output [5:0] _7,
  output [5:0] _1,
  output [5:0] _2,
  output [5:0] _3,
  output Overflow
);

  wire and_1_out, and_2_out, and_3_out, and_4_out, and_5_out, and_6_out, and_7_out, controlled_buffer_1_out,
       not_1_out, not_2_out, not_3_out, not_4_out, not_5_out, not_6_out, not_7_out, not_8_out, not_9_out,
       not_10_out, not_11_out, not_12_out, not_13_out;
  wire [2:0] counter_1_q;

  assign controlled_buffer_1_out = not_1_out ? Clock : 1'bz;  // Controlled_Buffer controlled_buffer_1
  Counter #(.width(3), .max('h7), .ongoal("stay")) counter_1 (
    .Q(counter_1_q), .carry(Overflow), .clk(controlled_buffer_1_out), .clr(Clear));  // open: load, D, count
  not not_1 (not_1_out, Overflow);
  and and_1 (and_1_out, not_2_out, not_4_out, not_3_out);
  not not_2 (not_2_out, counter_1_q[0]);
  not not_3 (not_3_out, counter_1_q[2]);
  not not_4 (not_4_out, counter_1_q[1]);
  and and_2 (and_2_out, counter_1_q[0], not_5_out, not_6_out);
  not not_5 (not_5_out, counter_1_q[1]);
  not not_6 (not_6_out, counter_1_q[2]);
  assign _4 = and_4_out ? \Posição  : 6'bz;  // Controlled_Buffer controlled_buffer_2
  assign _1 = and_1_out ? \Posição  : 6'bz;  // Controlled_Buffer controlled_buffer_3
  and and_3 (and_3_out, not_8_out, counter_1_q[1], not_7_out);
  not not_7 (not_7_out, counter_1_q[2]);
  not not_8 (not_8_out, counter_1_q[0]);
  and and_4 (and_4_out, counter_1_q[0], counter_1_q[1], not_9_out);
  not not_9 (not_9_out, counter_1_q[2]);
  not not_10 (not_10_out, counter_1_q[0]);
  assign _5 = and_5_out ? \Posição  : 6'bz;  // Controlled_Buffer controlled_buffer_4
  assign _2 = and_2_out ? \Posição  : 6'bz;  // Controlled_Buffer controlled_buffer_5
  and and_5 (and_5_out, not_10_out, not_11_out, counter_1_q[2]);
  and and_6 (and_6_out, counter_1_q[0], not_12_out, counter_1_q[2]);
  not not_11 (not_11_out, counter_1_q[1]);
  not not_12 (not_12_out, counter_1_q[1]);
  assign _6 = and_6_out ? \Posição  : 6'bz;  // Controlled_Buffer controlled_buffer_6
  assign _3 = and_3_out ? \Posição  : 6'bz;  // Controlled_Buffer controlled_buffer_7
  and and_7 (and_7_out, not_13_out, counter_1_q[1], counter_1_q[2]);
  not not_13 (not_13_out, counter_1_q[0]);
  assign _7 = and_7_out ? \Posição  : 6'bz;  // Controlled_Buffer controlled_buffer_8
endmodule

module Comparador_Geral (
  input  Enable,
  input  [5:0] _1,
  input  [5:0] _2,
  input  [5:0] _3,
  input  [5:0] _4,
  input  [5:0] _5,
  input  [5:0] _6,
  input  [5:0] _7,
  output Saida
);

  wire comparator_1_eq, comparator_2_eq, comparator_3_eq, comparator_4_eq, comparator_5_eq, comparator_6_eq,
       comparator_7_eq, comparator_8_eq, comparator_9_eq, comparator_10_eq, comparator_11_eq,
       comparator_12_eq, comparator_13_eq, comparator_14_eq, comparator_15_eq, comparator_16_eq,
       comparator_17_eq, comparator_18_eq, comparator_19_eq, comparator_20_eq, comparator_21_eq, or_1_out,
       or_2_out, or_3_out, or_4_out, or_5_out, or_6_out;

  Comparator #(.width(6)) comparator_1 (.a(_1), .b(_2), .eq(comparator_1_eq));  // open: gt, lt
  Comparator #(.width(6)) comparator_2 (.a(_1), .b(_3), .eq(comparator_2_eq));  // open: gt, lt
  Comparator #(.width(6)) comparator_3 (.a(_1), .b(_4), .eq(comparator_3_eq));  // open: gt, lt
  Comparator #(.width(6)) comparator_4 (.a(_1), .b(_5), .eq(comparator_4_eq));  // open: gt, lt
  Comparator #(.width(6)) comparator_5 (.a(_1), .b(_6), .eq(comparator_5_eq));  // open: gt, lt
  Comparator #(.width(6)) comparator_6 (.a(_1), .b(_7), .eq(comparator_6_eq));  // open: gt, lt
  or or_1 (or_1_out, comparator_1_eq, comparator_2_eq, comparator_3_eq, comparator_4_eq, comparator_5_eq, comparator_6_eq);
  Comparator #(.width(6)) comparator_7 (.a(_2), .b(_3), .eq(comparator_7_eq));  // open: gt, lt
  Comparator #(.width(6)) comparator_8 (.a(_2), .b(_4), .eq(comparator_8_eq));  // open: gt, lt
  Comparator #(.width(6)) comparator_9 (.a(_2), .b(_5), .eq(comparator_9_eq));  // open: gt, lt
  Comparator #(.width(6)) comparator_10 (.a(_2), .b(_6), .eq(comparator_10_eq));  // open: gt, lt
  Comparator #(.width(6)) comparator_11 (.a(_2), .b(_7), .eq(comparator_11_eq));  // open: gt, lt
  or or_2 (or_2_out, comparator_7_eq, comparator_8_eq, comparator_9_eq, comparator_10_eq, comparator_11_eq);
  Comparator #(.width(6)) comparator_12 (.a(_3), .b(_4), .eq(comparator_12_eq));  // open: gt, lt
  Comparator #(.width(6)) comparator_13 (.a(_3), .b(_5), .eq(comparator_13_eq));  // open: gt, lt
  or or_3 (or_3_out, comparator_12_eq, comparator_13_eq, comparator_14_eq, comparator_15_eq);
  Comparator #(.width(6)) comparator_14 (.a(_3), .b(_6), .eq(comparator_14_eq));  // open: gt, lt
  Comparator #(.width(6)) comparator_15 (.a(_3), .b(_7), .eq(comparator_15_eq));  // open: gt, lt
  assign Saida = Enable ? or_4_out : 1'bz;  // Controlled_Buffer controlled_buffer_1
  or or_4 (or_4_out, or_1_out, or_2_out, or_3_out, or_5_out, or_6_out, comparator_21_eq);
  Comparator #(.width(6)) comparator_16 (.a(_4), .b(_5), .eq(comparator_16_eq));  // open: gt, lt
  Comparator #(.width(6)) comparator_17 (.a(_4), .b(_6), .eq(comparator_17_eq));  // open: gt, lt
  or or_5 (or_5_out, comparator_16_eq, comparator_17_eq, comparator_18_eq);
  Comparator #(.width(6)) comparator_18 (.a(_4), .b(_7), .eq(comparator_18_eq));  // open: gt, lt
  Comparator #(.width(6)) comparator_19 (.a(_5), .b(_6), .eq(comparator_19_eq));  // open: gt, lt
  Comparator #(.width(6)) comparator_20 (.a(_5), .b(_7), .eq(comparator_20_eq));  // open: gt, lt
  or or_6 (or_6_out, comparator_19_eq, comparator_20_eq);
  Comparator #(.width(6)) comparator_21 (.a(_6), .b(_7), .eq(comparator_21_eq));  // open: gt, lt
endmodule

module Comparador_Truco (
  input  [3:0] Carta_1,
  input  [5:0] \Posição_1 ,
  input  [3:0] Coringa_Carta,
  input  [3:0] Carta_2,
  input  [5:0] \Posição_2 ,
  output Clock_1,
  output Clock_2,
  output Embuchada
);

  wire and_1_out, and_2_out, and_3_out, and_4_out, comparador_naipes_1_clock_1, comparador_naipes_1_clock_2,
       comparator_1_eq, comparator_1_gt, comparator_1_lt, comparator_2_eq, comparator_2_gt, comparator_2_lt,
       comparator_3_eq, comparator_3_gt, comparator_3_lt, comparator_4_eq, comparator_4_gt, comparator_4_lt,
       comparator_5_eq, comparator_5_gt, comparator_5_lt, comparator_6_eq, comparator_6_gt, comparator_6_lt,
       or_1_out, or_2_out, or_3_out, or_4_out, or_5_out, xor_1_out, xor_2_out;
  wire [3:0] adder_1_out, controlled_buffer_1_out, controlled_buffer_10_out, controlled_buffer_11_out,
       controlled_buffer_12_out, controlled_buffer_13_out;

  Comparator #(.width(4)) comparator_1 (
    .a(Coringa_Carta), .b(4'b1010), .gt(comparator_1_gt), .eq(comparator_1_eq), .lt(comparator_1_lt));
  assign controlled_buffer_1_out = comparator_1_eq ? 4'b0001 : 4'bz;  // Controlled_Buffer controlled_buffer_1
  Adder #(.width(4)) adder_1 (.a(Coringa_Carta), .b(4'b0001), .out(adder_1_out));  // open: cin, cout
  or or_1 (or_1_out, comparator_1_gt, comparator_1_lt);
  assign controlled_buffer_1_out = or_1_out ? adder_1_out : 4'bz;  // Controlled_Buffer controlled_buffer_2
  Comparator #(.width(4)) comparator_2 (
    .a(controlled_buffer_1_out), .b(Carta_1), .gt(comparator_2_gt), .eq(comparator_2_eq), .lt(comparator_2_lt));
  Comparator #(.width(4)) comparator_3 (
    .a(Carta_2), .b(controlled_buffer_1_out), .gt(comparator_3_gt), .eq(comparator_3_eq), .lt(comparator_3_lt));
  assign Clock_1 = and_1_out ? comparador_naipes_1_clock_1 : 1'bz;  // Controlled_Buffer controlled_buffer_3
  or or_2 (or_2_out, comparator_2_gt, comparator_2_lt);
  Comparador_Naipes comparador_naipes_1 (
    .Clock_1(comparador_naipes_1_clock_1), .\Posição_1 (\Posição_1 ), .\Posição_2 (\Posição_2 ),
    .Clock_2(comparador_naipes_1_clock_2));
  and and_1 (and_1_out, comparator_2_eq, comparator_3_eq);
  or or_3 (or_3_out, comparator_3_gt, comparator_3_lt);
  assign Clock_2 = and_1_out ? comparador_naipes_1_clock_2 : 1'bz;  // Controlled_Buffer controlled_buffer_4
  assign Clock_1 = xor_1_out ? comparator_2_eq : 1'bz;  // Controlled_Buffer controlled_buffer_5
  assign Clock_2 = xor_1_out ? comparator_3_eq : 1'bz;  // Controlled_Buffer controlled_buffer_6
  assign Embuchada = and_2_out ? comparator_6_eq : 1'bz;  // Controlled_Buffer controlled_buffer_7
  and and_2 (and_2_out, or_2_out, or_3_out);
  assign Clock_1 = and_2_out ? comparator_6_gt : 1'bz;  // Controlled_Buffer controlled_buffer_8
  xor xor_1 (xor_1_out, comparator_2_eq, comparator_3_eq);
  assign Clock_2 = and_2_out ? comparator_6_lt : 1'bz;  // Controlled_Buffer controlled_buffer_9
  and and_3 (and_3_out, comparator_4_lt, comparator_5_lt);
  Comparator #(.width(4), .mode("unsigned")) comparator_4 (
    .a(4'b0011), .b(Carta_1), .gt(comparator_4_gt), .eq(comparator_4_eq), .lt(comparator_4_lt));
  assign controlled_buffer_10_out = and_3_out ? Carta_1 : 4'bz;  // Controlled_Buffer controlled_buffer_10
  assign controlled_buffer_11_out = and_3_out ? Carta_2 : 4'bz;  // Controlled_Buffer controlled_buffer_11
  Comparator #(.width(4), .mode("unsigned")) comparator_5 (
    .a(4'b0011), .b(Carta_2), .gt(comparator_5_gt), .eq(comparator_5_eq), .lt(comparator_5_lt));
  or or_4 (or_4_out, comparator_4_gt, comparator_4_eq);
  and and_4 (and_4_out, or_4_out, or_5_out);
  Comparator #(.width(4), .mode("unsigned")) comparator_6 (
    .a(controlled_buffer_10_out), .b(controlled_buffer_11_out), .gt(comparator_6_gt), .eq(comparator_6_eq),
    .lt(comparator_6_lt));
  or or_5 (or_5_out, comparator_5_gt, comparator_5_eq);
  assign controlled_buffer_12_out = and_4_out ? Carta_1 : 4'bz;  // Controlled_Buffer controlled_buffer_12
  assign controlled_buffer_13_out = and_4_out ? Carta_2 : 4'bz;  // Controlled_Buffer controlled_buffer_13
  assign comparator_6_gt = xor_2_out ? ~comparator_4_lt : 1'bz;  // Controlled_Inverter controlled_inverter_1
  Comparator #(.width(4), .mode("unsigned")) comparator_7 (
    .a(controlled_buffer_12_out), .b(controlled_buffer_13_out), .gt(comparator_6_gt), .eq(comparator_6_eq),
    .lt(comparator_6_lt));
  assign comparator_6_lt = xor_2_out ? ~comparator_5_lt : 1'bz;  // Controlled_Inverter controlled_inverter_2
  xor xor_2 (xor_2_out, comparator_4_lt, comparator_5_lt);
endmodule

module Comparador_Naipes (
  input  [5:0] \Posição_1 ,
  input  [5:0] \Posição_2 ,
  output Clock_1,
  output Clock_2
);

  wire [5:0] divider_1_rem, divider_2_rem;

  Divider #(.width(6)) divider_1 (.a(\Posição_1 ), .b(6'b000100), .rem(divider_1_rem));  // open: out, upper
  Divider #(.width(6)) divider_2 (.a(\Posição_2 ), .b(6'b000100), .rem(divider_2_rem));  // open: out, upper
  Comparator #(.width(6)) comparator_1 (.a(divider_1_rem), .b(divider_2_rem), .gt(Clock_1), .lt(Clock_2));  // open: eq
endmodule
