// Logisim project 1)a).circ as structural Verilog: 1 circuit, main circuit main
module main (
  input  X,
  input  Y,
  input  M,
  output out_4
);

  wire and_1_out, nand_1_out, or_1_out, or_2_out, or_3_out, or_4_out;

  or or_1 (or_1_out, X, Y);
  or or_2 (or_2_out, or_1_out, M);
  or or_3 (or_3_out, X, Y, M);
  nand nand_1 (nand_1_out, X, Y, M);
  or or_4 (or_4_out, or_3_out, nand_1_out);
  and and_1 (and_1_out, or_2_out, or_4_out);
  or or_5 (out_4, and_1_out, M);
endmodule
