// Logisim project Ex 1 Respostas Sistemas.circ as structural Verilog: 1 circuit, main circuit main
module main (
  input  X,
  input  X_2,
  input  Y,
  input  Y_2,
  input  X_3,
  input  Z,
  input  Y_3,
  input  M,
  input  Z_2,
  input  X_4,
  input  c,
  input  Y_4,
  input  Z_3,
  input  in_14,
  input  X_5,
  input  X_6,
  input  Y_5,
  input  Z_4,
  input  Y_6,
  input  Z_5,
  input  X_7,
  input  Y_7,
  output out_23,
  output out_24,
  output out_25,
  output out_26,
  output out_27,
  output out_28,
  output out_29,
  output out_30
);

  wire and_1_out, and_2_out, and_4_out, and_5_out, and_6_out, not_1_out, not_2_out, not_3_out, not_4_out,
       not_5_out, not_6_out, not_7_out, not_8_out, or_2_out, or_3_out, or_4_out, or_8_out, or_9_out,
       or_11_out;

  not not_1 (not_1_out, Y);
  not not_2 (not_2_out, Y_3);
  not not_3 (not_3_out, in_14);
  not not_4 (not_4_out, X_6);
  not not_5 (not_5_out, Y_6);
  or or_1 (out_23, X, not_1_out);
  and and_1 (and_1_out, X_3, not_2_out);
  or or_2 (or_2_out, c, in_14);
  or or_3 (or_3_out, c, not_3_out);
  and and_2 (and_2_out, not_4_out, not_5_out);
  or or_4 (or_4_out, not_4_out, Z_5);
  or or_5 (out_25, and_1_out, Z_2);
  not not_6 (not_6_out, and_2_out);
  or or_6 (out_29, not_6_out, or_4_out);
  and and_3 (out_27, or_2_out, or_3_out);
  not not_7 (not_7_out, X_2);
  and and_4 (and_4_out, Y_4, Z_3);
  and and_5 (and_5_out, X_7, Y_7);
  and and_6 (and_6_out, not_7_out, Y_2, Z);
  or or_7 (out_26, X_4, and_4_out);
  or or_8 (or_8_out, X_5, Y_5);
  or or_9 (or_9_out, X_5, Z_4);
  or or_10 (out_30, X_7, and_5_out);
  not not_8 (not_8_out, or_11_out);
  or or_11 (or_11_out, X_2, M);
  and and_7 (out_28, or_8_out, or_9_out);
  and and_8 (out_24, and_6_out, not_8_out);

  // Notes on the sheet:
  //   a)
  //   b)
  //   d)
  //   e)
  //   g)
  //   h)
  //   f)
endmodule
