// Logisim project Ex 3 Respostas Sistemas.circ as structural Verilog: 1 circuit, main circuit main
module main (
  input  _2_Chaves,
  input  in_2,
  input  _3_Chaves,
  input  in_4,
  input  in_5,
  output out_6,
  output out_7
);

  wire xor_2_out;

  xor xor_1 (out_6, _2_Chaves, in_2);
  xor xor_2 (xor_2_out, _3_Chaves, in_4);
  xor xor_3 (out_7, xor_2_out, in_5);
endmodule
