// Logisim project 1)b).circ as structural Verilog: 1 circuit, main circuit main
module main (
  input  in_1,
  input  in_2,
  input  M,
  input  X,
  input  in_5,
  output out_6
);

  wire and_1_out, nand_1_out, or_1_out, or_2_out, or_3_out, or_4_out;

  or or_1 (or_1_out, in_1, in_2);
  or or_2 (or_2_out, or_1_out, M);
  or or_3 (or_3_out, M, in_5);
  nand nand_1 (nand_1_out, in_2, X, M);
  or or_4 (or_4_out, or_3_out, nand_1_out);
  and and_1 (and_1_out, or_2_out, or_4_out);
  and and_2 (out_6, and_1_out, M);
endmodule
